// Logisim project Brick_Game_Main.circ as structural Verilog: 6 circuits, main circuit main
module main (
);

  wire button_2_out, button_3_out, button_4_out, button_5_out, button_6_out, button_out, cpu_1_out_6,
       keyboard_1_avail;
  wire [3:0] key_1_out_5;
  wire [6:0] keyboard_1_data;
  wire [15:0] cpu_1_out_17, cpu_1_out_18;
  wire [19:0] cpu_1_out_7, cpu_1_out_8, cpu_1_out_9, cpu_1_out_10, cpu_1_out_11, cpu_1_out_12, cpu_1_out_13,
       cpu_1_out_14, cpu_1_out_15, cpu_1_out_16;

  Keyboard keyboard_1 (.clk(cpu_1_out_6), .avail(keyboard_1_avail), .data(keyboard_1_data));  // open: re, clr
  CPU cpu_1 (
    .out_7(cpu_1_out_7), .out_8(cpu_1_out_8), .out_9(cpu_1_out_9), .out_10(cpu_1_out_10),
    .out_11(cpu_1_out_11), .out_12(cpu_1_out_12), .out_13(cpu_1_out_13), .out_14(cpu_1_out_14),
    .out_15(cpu_1_out_15), .out_16(cpu_1_out_16), .out_17(cpu_1_out_17), .out_18(cpu_1_out_18),
    .in_5(button_6_out), .in_2(button_5_out), .\Кнопка (key_1_out_5), .out_6(cpu_1_out_6),
    .in_3(keyboard_1_avail), .in_1(keyboard_1_data));
  DotMatrix #(.matrixcols(10), .matrixrows(20)) dotmatrix_1 (
    .col0(cpu_1_out_7), .col1(cpu_1_out_8), .col2(cpu_1_out_9), .col3(cpu_1_out_10), .col4(cpu_1_out_11),
    .col5(cpu_1_out_12), .col6(cpu_1_out_13), .col7(cpu_1_out_14), .col8(cpu_1_out_15), .col9(cpu_1_out_16));
  Button button (.out(button_out));
  Key key_1 (.in_1(button_out), .in_2(button_3_out), .in_3(button_2_out), .in_4(button_4_out), .out_5(key_1_out_5));
  Button button_2 (.out(button_2_out));
  Button button_3 (.out(button_3_out));
  Button button_4 (.out(button_4_out));
  Button button_5 (.out(button_5_out));
  // Probe on cpu_1_out_17
  // Probe on cpu_1_out_18
  Button button_6 (.out(button_6_out));

  // Notes on the sheet:
  //   Brick Game
endmodule

module CPU (
  input  [6:0] in_1,
  input  in_2,
  input  in_3,
  input  [3:0] \Кнопка ,
  input  in_5,
  output out_6,
  output [19:0] out_7,
  output [19:0] out_8,
  output [19:0] out_9,
  output [19:0] out_10,
  output [19:0] out_11,
  output [19:0] out_12,
  output [19:0] out_13,
  output [19:0] out_14,
  output [19:0] out_15,
  output [19:0] out_16,
  output [15:0] out_17,
  output [15:0] out_18
);

  wire _0xF0_out, _0xF1_out, _0xF2_out, _0xF3_out, _0xF4_out, _0xF5_out, _0xF6_out, and_1_out, and_2_out,
       and_3_out, and_4_out, car_oper_1_on_off, cars, cdm_8_1_data_code_prime, cdm_8_1_load_st_prime,
       cdm_8_1_mem, Cl, comparator_1_eq, comparator_6_eq, comparator_7_gt, controlled_buffer_1_out,
       cpu_snake_1_p1, decoder_1_out0, decoder_1_out1, decoder_3_out0, decoder_3_out1, decoder_3_out2,
       decoder_3_out3, decoder_3_out4, decoder_3_out5, decoder_3_out6, decoder_4_out0, decoder_4_out1,
       decoder_4_out2, E, Game, not_2_out, not_3_out, not_4_out, or_4_out, or_5_out, or_6_out,
       pull_resistor_6_node, register_1_q, reset, sbros, snake, Space, space_t;
  wire [1:0] mod;
  wire [3:0] comparator_2_eq, controlled_buffer_3_out, Key;
  wire [4:4] pull_resistor_5_node;
  wire [7:0] cdm_8_1_data_out, cdm_8_1_pc, cdm_8_1_r0, cdm_8_1_r1, cdm_8_1_r2, cdm_8_1_r3, cdm_8_1_sp,
       controlled_buffer_2_out, Input_0xF3, Input_0xF4, Input_0xF5, Input_0xF6, Output_0xF0, Output_0xF1,
       Output_0xF2, pull_resistor_2_node, \обратный_буфер_1_out_3 ;
  wire [15:0] car_oper_1_out_15, controlled_buffer_8_out;
  wire [19:0] car_oper_1_disp0, car_oper_1_disp1, car_oper_1_disp2, car_oper_1_disp3, car_oper_1_disp4,
       car_oper_1_disp5, car_oper_1_disp6, car_oper_1_disp7, car_oper_1_disp8, car_oper_1_disp9;

  Clock clock_1 (.out(Cl));
  not not_1 (sbros, register_1_q);
  // Probe on cdm_8_1_r0
  assign controlled_buffer_1_out = and_1_out ? Cl : 1'bz;  // Controlled_Buffer controlled_buffer_1
  not not_2 (not_2_out, Game);
  and and_1 (and_1_out, register_1_q, Game);
  Register #(.width(1)) register_1 (.D(sbros), .Q(register_1_q), .clk(reset), .clr(Output_0xF0[6]));  // open: en
  Comparator #(.width(7)) comparator_1 (.a(in_1), .b(7'b0100000), .eq(comparator_1_eq));  // open: gt, lt
  Comparator #(.width(7)) comparator_2 (.a(in_1), .b(7'b1110111), .eq(comparator_2_eq[0]));  // open: gt, lt
  Comparator #(.width(7)) comparator_3 (.a(in_1), .b(7'b1100100), .eq(comparator_2_eq[1]));  // open: gt, lt
  Comparator #(.width(7)) comparator_4 (.a(in_1), .b(7'b1100001), .eq(comparator_2_eq[2]));  // open: gt, lt
  Comparator #(.width(7)) comparator_5 (.a(in_1), .b(7'b1110011), .eq(comparator_2_eq[3]));  // open: gt, lt
  Comparator #(.width(7)) comparator_6 (.a(in_1), .b(7'b1100101), .eq(comparator_6_eq));  // open: gt, lt
  // Probe on cdm_8_1_r3
  // Probe on cdm_8_1_r2
  // Probe on cdm_8_1_pc
  // Probe on cdm_8_1_r1
  or or_1 (space_t, comparator_1_eq, in_2);
  assign Key = \Кнопка  | comparator_2_eq;  // OR_Gate or_2, 4 bits wide
  or or_3 (E, comparator_6_eq, in_5);
  // Probe on cdm_8_1_sp
  Pull_Resistor pull_resistor_1 (.node(controlled_buffer_1_out));
  Decoder #(.disabled(0)) decoder_1 (
    .out0(decoder_1_out0), .out1(decoder_1_out1), .sel(cdm_8_1_data_code_prime), .en(cdm_8_1_mem));
  Pull_Resistor pull_resistor_2 (.node(pull_resistor_2_node));
  CdM_8 cdm_8_1 (
    .data_code_prime(cdm_8_1_data_code_prime), .R0(cdm_8_1_r0), .R1(cdm_8_1_r1), .mem(cdm_8_1_mem),
    .R2(cdm_8_1_r2), .load_st_prime(cdm_8_1_load_st_prime), .R3(cdm_8_1_r3), .addr(pull_resistor_2_node),
    .PC(cdm_8_1_pc), .SP(cdm_8_1_sp), .data_out(cdm_8_1_data_out), .data_in(controlled_buffer_2_out),
    .clk(controlled_buffer_1_out), .rset(not_2_out));  // open: page, PS, IAck, IRQ, vector, shadow
  assign controlled_buffer_2_out = cdm_8_1_load_st_prime ? \обратный_буфер_1_out_3  : 8'bz;  // Controlled_Buffer controlled_buffer_2
  assign controlled_buffer_3_out = not_3_out ? Key : 4'bz;  // Controlled_Buffer controlled_buffer_3
  not not_3 (not_3_out, Game);
  \обратный_буфер  \u_обратный_буфер_1  (
    .in_1(cdm_8_1_data_out), .in_2(cdm_8_1_load_st_prime), .out_3(\обратный_буфер_1_out_3 ));
  or or_4 (or_4_out, controlled_buffer_3_out[2], controlled_buffer_3_out[1]);
  Pull_Resistor pull_resistor_3 (.node(controlled_buffer_3_out));
  and and_2 (and_2_out, ~Game, space_t);  // AND_Gate
  and and_3 (and_3_out, decoder_1_out1, controlled_buffer_1_out, comparator_7_gt);
  Comparator #(.mode("unsigned")) comparator_7 (
    .a(pull_resistor_2_node), .b(8'hef), .gt(comparator_7_gt));  // open: eq, lt
  Pull_Resistor pull_resistor_4 (.node(mod));
  Counter #(.width(2), .max('h2)) counter_1 (
    .load(controlled_buffer_3_out[2]), .Q(mod), .clk(or_4_out));  // open: D, count, carry, clr
  not not_4 (not_4_out, Game);
  Register #(.width(1), .trigger("falling")) register_2 (.D(not_4_out), .Q(Game), .clk(or_5_out));  // open: en, clr
  or or_5 (or_5_out, and_2_out, and_4_out);
  and and_4 (and_4_out, Game, E, or_6_out);
  Decoder #(.select(2), .disabled(0)) decoder_2 (
    .out0(Space), .out1(cars), .out2(snake), .sel(mod), .en(decoder_1_out0));  // open: out3
  Pull_Resistor pull_resistor_5 (.node({pull_resistor_5_node[4], pull_resistor_2_node[3:0]}));
  Decoder #(.select(5), .disabled(0)) decoder_3 (
    .out0(decoder_3_out0), .out1(decoder_3_out1), .out2(decoder_3_out2), .out3(decoder_3_out3),
    .out4(decoder_3_out4), .out5(decoder_3_out5), .out6(decoder_3_out6),
    .sel({pull_resistor_5_node[4], pull_resistor_2_node[3:0]}), .en(and_3_out));  // open: out7, out8, out9, out10, out11, out12, out13, out14, out15, out16, out17, out18, out19, out20, out21, out22, out23, out24, out25, out26, out27, out28, out29, out30, out31
  ROM rom_1 (.addr(pull_resistor_2_node), .data(\обратный_буфер_1_out_3 ), .sel(Space));
  ROM rom_2 (.addr(pull_resistor_2_node), .data(\обратный_буфер_1_out_3 ), .sel(cars));
  ROM rom_3 (.addr(pull_resistor_2_node), .data(\обратный_буфер_1_out_3 ), .sel(snake));
  image image_1 (
    .in_11(mod), .out_14(out_7), .out_15(out_8), .out_16(out_9), .out_17(out_10), .out_18(out_11),
    .out_19(out_12), .out_20(out_13), .out_21(out_14), .out_22(out_15), .out_23(out_16), .in_12(Game),
    .in_1(car_oper_1_disp0), .in_2(car_oper_1_disp1), .in_3(car_oper_1_disp2), .in_4(car_oper_1_disp3),
    .in_5(car_oper_1_disp4), .in_6(car_oper_1_disp5), .in_7(car_oper_1_disp6), .in_8(car_oper_1_disp7),
    .in_9(car_oper_1_disp8), .in_10(car_oper_1_disp9), .in_13(or_6_out));
  car_oper car_oper_1 (
    .key(Key), .Disp0(car_oper_1_disp0), .Disp1(car_oper_1_disp1), .Disp2(car_oper_1_disp2),
    .Disp3(car_oper_1_disp3), .Disp4(car_oper_1_disp4), .Disp5(car_oper_1_disp5), .Disp6(car_oper_1_disp6),
    .Disp7(car_oper_1_disp7), .Disp8(car_oper_1_disp8), .Disp9(car_oper_1_disp9), .out_15(car_oper_1_out_15),
    .ON_OFF(car_oper_1_on_off), .in_4({space_t, E, Cl}), .in_3(decoder_4_out1), .in_1(Output_0xF0),
    .out_16(Input_0xF3), .out_17(reset));
  and _0xF0 (_0xF0_out, decoder_3_out0, ~cdm_8_1_load_st_prime);  // AND_Gate
  and _0xF1 (_0xF1_out, decoder_3_out1, ~cdm_8_1_load_st_prime);  // AND_Gate
  and _0xF2 (_0xF2_out, decoder_3_out2, ~cdm_8_1_load_st_prime);  // AND_Gate
  and _0xF3 (_0xF3_out, decoder_3_out3, cdm_8_1_load_st_prime);
  and _0xF4 (_0xF4_out, decoder_3_out4, cdm_8_1_load_st_prime);
  and _0xF5 (_0xF5_out, decoder_3_out5, cdm_8_1_load_st_prime);
  and _0xF6 (_0xF6_out, decoder_3_out6, cdm_8_1_load_st_prime);
  Register register_3 (.D(\обратный_буфер_1_out_3 ), .Q(Output_0xF0), .clk(_0xF0_out), .clr(sbros));  // open: en
  Register register_4 (.D(\обратный_буфер_1_out_3 ), .Q(Output_0xF1), .clk(_0xF1_out));  // open: en, clr
  Register register_5 (.D(\обратный_буфер_1_out_3 ), .Q(Output_0xF2), .clk(_0xF2_out));  // open: en, clr
  assign \обратный_буфер_1_out_3  = _0xF3_out ? Input_0xF3 : 8'bz;  // Controlled_Buffer controlled_buffer_4
  assign \обратный_буфер_1_out_3  = _0xF4_out ? Input_0xF4 : 8'bz;  // Controlled_Buffer controlled_buffer_5
  assign \обратный_буфер_1_out_3  = _0xF5_out ? Input_0xF5 : 8'bz;  // Controlled_Buffer controlled_buffer_6
  assign \обратный_буфер_1_out_3  = _0xF6_out ? Input_0xF6 : 8'bz;  // Controlled_Buffer controlled_buffer_7
  assign controlled_buffer_8_out = decoder_4_out1 ? car_oper_1_out_15 : 16'bz;  // Controlled_Buffer controlled_buffer_8
  Decoder #(.select(2), .disabled(0)) decoder_4 (
    .out0(decoder_4_out0), .out1(decoder_4_out1), .out2(decoder_4_out2), .sel(mod), .en(Game));  // open: out3
  Best_Scores best_scores_1 (
    .in_1(mod), .out_7(out_18), .in_5(Cl), .in_2(controlled_buffer_8_out), .in_4(Game), .out_8(out_17),
    .in_3(or_6_out), .in_6(space_t));
  or or_6 (or_6_out, cpu_snake_1_p1, pull_resistor_6_node, car_oper_1_on_off);
  // CPU_snake cpu_snake_1: pin names not known; wires that end beside it: cpu_snake_1_p1, car_oper_1_disp0, car_oper_1_disp1, Key, car_oper_1_disp2, car_oper_1_disp3, Output_0xF0, car_oper_1_disp4, Output_0xF1, car_oper_1_disp5, reset, car_oper_1_disp6, Input_0xF4, car_oper_1_disp7, Input_0xF3, car_oper_1_disp8, car_oper_1_disp9, controlled_buffer_8_out, decoder_4_out2
  Pull_Resistor pull_resistor_6 (.node(pull_resistor_6_node));
  Test_main main_1 (
    .in_1(decoder_4_out0), .out_22(controlled_buffer_8_out), .CdM8(reset), .out_21(pull_resistor_6_node),
    .Frd(Input_0xF5), .Snd(Input_0xF4), .Fst(Input_0xF3), .inFromCdM8(Output_0xF0),
    .out_11(car_oper_1_disp4), .out_12(car_oper_1_disp5), .out_13(car_oper_1_disp6),
    .out_14(car_oper_1_disp7), .out_15(car_oper_1_disp8), .out_16(car_oper_1_disp9),
    .out_7(car_oper_1_disp0), .out_8(car_oper_1_disp1), .out_9(car_oper_1_disp2), .out_10(car_oper_1_disp3),
    .in_5(Key), .in_6(Cl), .in_4(space_t), .in_3(E));

  assign out_6 = in_3;

  // Other names for the same wires on the sheet: d0[19:0] = out_7; d1[19:0] = out_8; d2[19:0] = out_9;
  //   d3[19:0] = out_10; d4[19:0] = out_11; d5[19:0] = out_12; d6[19:0] = out_13; d7[19:0] = out_14;
  //   d8[19:0] = out_15; d9[19:0] = out_16; Key1[3:0] = Key

  // Notes on the sheet:
  //   contents of rom_1 (hex, n*v repeats v):
  //   d0 0 d1 0 d2 0 d3 0 d3 f3 bd d2 8 78 e0 1b d2 1 46 e0 17 ee 42 99 8c ee b 8f bd d2 10 78 e0 30 d2 1
  //   46 e0 2c 0 e0 2c ee 42 99 8c ee 1d 8f bd d2 14 78 e0 42 d2 1 46 e0 3e ee 42 99 8c ee 32 d3 f0 88 d2
  //   40 58 ac ee 0 d4
  //   contents of rom_2 (hex, n*v repeats v):
  //   d0 f3 b0 d1 4 d2 2 d3 1 41 e1 1e 42 e1 17 d1 f0 d3 40 5c a4 ee 1c d0 f0 d1 c0 a1 ee 2e 43 e1 29 d1
  //   f0 d3 40 5c a4 ee 2e d0 f0 d1 c0 a1 ee 0 d4
  //   contents of rom_3 (hex, n*v repeats v):
  //   d0 f3 b0 d1 f4 b5 d2 3 42 d3 3 47 1b d2 3 7e e1 17 d3 3 43 ee 1a d3 3 47 98 98 98 99 99 d2 3 7e e1
  //   27 89 ee 38 d2 2 7e e1 2f 88 ee 38 d2 1 7e e1 37 8c ee 38 8d 0 e5 3f d0 9 ee 46 d2 9 78 e5 46 d0 0 5
  //   e5 4d d1 13 ee 54 d2 13 79 e5 54 d1 0 95 95 1d d3 f1 ad d3 40 5c d2 f0 a8 ee 0 d4
endmodule

module Key (
  input  in_1,
  input  in_2,
  input  in_3,
  input  in_4,
  output [3:0] out_5
);


  assign out_5 = {in_4, in_3, in_2, in_1};
endmodule

module image (
  input  [19:0] in_1,
  input  [19:0] in_2,
  input  [19:0] in_3,
  input  [19:0] in_4,
  input  [19:0] in_5,
  input  [19:0] in_6,
  input  [19:0] in_7,
  input  [19:0] in_8,
  input  [19:0] in_9,
  input  [19:0] in_10,
  input  [1:0] in_11,
  input  in_12,
  input  in_13,
  output [19:0] out_14,
  output [19:0] out_15,
  output [19:0] out_16,
  output [19:0] out_17,
  output [19:0] out_18,
  output [19:0] out_19,
  output [19:0] out_20,
  output [19:0] out_21,
  output [19:0] out_22,
  output [19:0] out_23
);

  wire and_1_out;
  wire [19:0] multiplexer_1_out, multiplexer_2_out, multiplexer_3_out, multiplexer_4_out, multiplexer_5_out,
       multiplexer_6_out, multiplexer_7_out, multiplexer_8_out, multiplexer_9_out, multiplexer_10_out,
       multiplexer_11_out, multiplexer_12_out, multiplexer_13_out, multiplexer_14_out, multiplexer_15_out,
       multiplexer_16_out, multiplexer_17_out, multiplexer_18_out, multiplexer_19_out, multiplexer_20_out;

  Multiplexer #(.select(2), .width(20)) multiplexer_1 (
    .in0(20'h600), .in1(20'h777), .in2({20{1'b0}}), .out(multiplexer_1_out), .sel(in_11));  // open: in3, en
  Multiplexer #(.select(2), .width(20)) multiplexer_2 (
    .in0(20'ha00), .in1({20{1'b0}}), .in2(20'h70), .out(multiplexer_2_out), .sel(in_11));  // open: in3, en
  Multiplexer #(.select(2), .width(20)) multiplexer_3 (
    .in0(20'he00), .in1(20'h280), .in2(20'h10), .out(multiplexer_3_out), .sel(in_11));  // open: in3, en
  Multiplexer #(.select(2), .width(20)) multiplexer_4 (
    .in0(20'h1ee00), .in1(20'h3e700), .in2(20'h1c000), .out(multiplexer_4_out), .sel(in_11));  // open: in3, en
  Multiplexer #(.select(2), .width(20)) multiplexer_5 (
    .in0(20'h28400), .in1(20'h2a280), .in2(20'h22000), .out(multiplexer_5_out), .sel(in_11));  // open: in3, en
  Multiplexer #(.select(2), .width(20)) multiplexer_6 (
    .in0(20'h28801), .in1(20'h2a005), .in2(20'h22000), .out(multiplexer_6_out), .sel(in_11));  // open: in3, en
  Multiplexer #(.select(2), .width(20)) multiplexer_7 (
    .in0(20'h1ec23), .in1(20'h1600e), .in2(20'h22000), .out(multiplexer_7_out), .sel(in_11));  // open: in3, en
  Multiplexer #(.select(2), .width(20)) multiplexer_8 (
    .in0(20'h401), .in1(20'h5), .in2(20'h20), .out(multiplexer_8_out), .sel(in_11));  // open: in3, en
  Multiplexer #(.select(2), .width(20)) multiplexer_9 (
    .in0(20'he00), .in1({20{1'b0}}), .in2({20{1'b0}}), .out(multiplexer_9_out), .sel(in_11));  // open: in3, en
  Multiplexer #(.select(2), .width(20)) multiplexer_10 (
    .in0(20'ha00), .in1(20'h777), .in2({20{1'b0}}), .out(multiplexer_10_out), .sel(in_11));  // open: in3, en
  Pull_Resistor pull_resistor_1 (.node(in_12));
  Multiplexer #(.width(20)) multiplexer_11 (
    .in0(multiplexer_1_out), .in1(in_1), .out(multiplexer_11_out), .sel(in_12));  // open: en
  Multiplexer #(.width(20)) multiplexer_12 (
    .in0(multiplexer_2_out), .in1(in_2), .out(multiplexer_12_out), .sel(in_12));  // open: en
  Multiplexer #(.width(20)) multiplexer_13 (
    .in0(multiplexer_3_out), .in1(in_3), .out(multiplexer_13_out), .sel(in_12));  // open: en
  Multiplexer #(.width(20)) multiplexer_14 (
    .in0(multiplexer_4_out), .in1(in_4), .out(multiplexer_14_out), .sel(in_12));  // open: en
  Multiplexer #(.width(20)) multiplexer_15 (
    .in0(multiplexer_5_out), .in1(in_5), .out(multiplexer_15_out), .sel(in_12));  // open: en
  Multiplexer #(.width(20)) multiplexer_16 (
    .in0(multiplexer_6_out), .in1(in_6), .out(multiplexer_16_out), .sel(in_12));  // open: en
  Multiplexer #(.width(20)) multiplexer_17 (
    .in0(multiplexer_7_out), .in1(in_7), .out(multiplexer_17_out), .sel(in_12));  // open: en
  Multiplexer #(.width(20)) multiplexer_18 (
    .in0(multiplexer_8_out), .in1(in_8), .out(multiplexer_18_out), .sel(in_12));  // open: en
  Multiplexer #(.width(20)) multiplexer_19 (
    .in0(multiplexer_9_out), .in1(in_9), .out(multiplexer_19_out), .sel(in_12));  // open: en
  Multiplexer #(.width(20)) multiplexer_20 (
    .in0(multiplexer_10_out), .in1(in_10), .out(multiplexer_20_out), .sel(in_12));  // open: en
  Multiplexer #(.width(20)) multiplexer_21 (
    .in0(multiplexer_11_out), .in1({20{1'b0}}), .out(out_14), .sel(and_1_out));  // open: en
  Multiplexer #(.width(20)) multiplexer_22 (
    .in0(multiplexer_12_out), .in1(20'hf0000), .out(out_15), .sel(and_1_out));  // open: en
  Multiplexer #(.width(20)) multiplexer_23 (
    .in0(multiplexer_13_out), .in1(20'h17800), .out(out_16), .sel(and_1_out));  // open: en
  Multiplexer #(.width(20)) multiplexer_24 (
    .in0(multiplexer_14_out), .in1(20'h14800), .out(out_17), .sel(and_1_out));  // open: en
  Multiplexer #(.width(20)) multiplexer_25 (
    .in0(multiplexer_15_out), .in1(20'h14b40), .out(out_18), .sel(and_1_out));  // open: en
  Multiplexer #(.width(20)) multiplexer_26 (
    .in0(multiplexer_16_out), .in1(20'h7b5f), .out(out_19), .sel(and_1_out));  // open: en
  Multiplexer #(.width(20)) multiplexer_27 (
    .in0(multiplexer_17_out), .in1(20'h2d5), .out(out_20), .sel(and_1_out));  // open: en
  Multiplexer #(.width(20)) multiplexer_28 (
    .in0(multiplexer_18_out), .in1(20'h2d5), .out(out_21), .sel(and_1_out));  // open: en
  Multiplexer #(.width(20)) multiplexer_29 (
    .in0(multiplexer_19_out), .in1(20'h11), .out(out_22), .sel(and_1_out));  // open: en
  Multiplexer #(.width(20)) multiplexer_30 (
    .in0(multiplexer_20_out), .in1({20{1'b0}}), .out(out_23), .sel(and_1_out));  // open: en
  and and_1 (and_1_out, in_12, in_13);
endmodule

module Best_Scores (
  input  [1:0] in_1,
  input  [15:0] in_2,
  input  in_3,
  input  in_4,
  input  in_5,
  input  in_6,
  output [15:0] out_7,
  output [15:0] out_8
);

  wire comparator_1_lt, comparator_2_lt, controlled_buffer_1_out, controlled_buffer_2_out,
       controlled_buffer_3_out, controlled_buffer_4_out, controlled_buffer_5_out, decoder_1_out0,
       decoder_1_out1, decoder_1_out2, decoder_1_out3, or_1_out;
  wire [15:0] demultiplexer_1_out0, demultiplexer_1_out1, demultiplexer_1_out2, demultiplexer_1_out3,
       multiplexer_1_out, multiplexer_3_out, register_1_q, register_2_q, register_3_q, register_4_q,
       register_5_q;

  Decoder #(.select(2), .enable("false")) decoder_1 (
    .out0(decoder_1_out0), .out1(decoder_1_out1), .out2(decoder_1_out2), .out3(decoder_1_out3), .sel(in_1));
  Demultiplexer #(.select(2), .width(16), .disabled(0), .enable("false")) demultiplexer_1 (
    .out0(demultiplexer_1_out0), .out1(demultiplexer_1_out1), .out2(demultiplexer_1_out2),
    .out3(demultiplexer_1_out3), .in(out_7), .sel(in_1));
  Register #(.width(16)) register_1 (
    .D(demultiplexer_1_out0), .Q(register_1_q), .clk(controlled_buffer_1_out));  // open: en, clr
  assign controlled_buffer_1_out = decoder_1_out0 ? controlled_buffer_5_out : 1'bz;  // Controlled_Buffer controlled_buffer_1
  Register #(.width(16)) register_2 (
    .D(demultiplexer_1_out1), .Q(register_2_q), .clk(controlled_buffer_2_out));  // open: en, clr
  assign controlled_buffer_2_out = decoder_1_out1 ? controlled_buffer_5_out : 1'bz;  // Controlled_Buffer controlled_buffer_2
  Register #(.width(16)) register_3 (
    .D(demultiplexer_1_out2), .Q(register_3_q), .clk(controlled_buffer_3_out));  // open: en, clr
  assign controlled_buffer_3_out = decoder_1_out2 ? controlled_buffer_5_out : 1'bz;  // Controlled_Buffer controlled_buffer_3
  Register #(.width(16)) register_4 (
    .D(demultiplexer_1_out3), .Q(register_4_q), .clk(controlled_buffer_4_out));  // open: en, clr
  assign controlled_buffer_4_out = decoder_1_out3 ? controlled_buffer_5_out : 1'bz;  // Controlled_Buffer controlled_buffer_4
  assign controlled_buffer_5_out = in_4 ? in_5 : 1'bz;  // Controlled_Buffer controlled_buffer_5
  Multiplexer #(.select(2), .width(16), .enable("false")) multiplexer_1 (
    .in0(register_1_q), .in1(register_2_q), .in2(register_3_q), .in3(register_4_q), .out(multiplexer_1_out),
    .sel(in_1));
  Multiplexer #(.width(16), .enable("false")) multiplexer_2 (
    .in0(multiplexer_1_out), .in1(out_8), .out(out_7), .sel(comparator_1_lt));
  Comparator #(.width(16), .mode("unsigned")) comparator_1 (
    .a(multiplexer_1_out), .b(out_8), .lt(comparator_1_lt));  // open: gt, eq
  Multiplexer #(.width(16), .disabled(0), .enable("false")) multiplexer_3 (
    .in0(in_2), .in1(register_5_q), .out(multiplexer_3_out), .sel(comparator_2_lt));
  Comparator #(.width(16), .mode("unsigned")) comparator_2 (
    .a(in_2), .b(register_5_q), .lt(comparator_2_lt));  // open: gt, eq
  Register #(.width(16)) register_5 (.D(multiplexer_3_out), .Q(register_5_q), .clk(in_5), .clr(or_1_out));  // open: en
  or or_1 (or_1_out, ~in_4, in_6);  // OR_Gate
  Multiplexer #(.width(16), .enable("false")) multiplexer_4 (.in0(in_2), .in1(register_5_q), .out(out_8), .sel(in_3));
endmodule

module \обратный_буфер  (
  input  [7:0] in_1,
  input  in_2,
  output [7:0] out_3
);

  wire not_1_out;

  not not_1 (not_1_out, in_2);
  assign out_3 = not_1_out ? in_1 : 8'bz;  // Controlled_Buffer controlled_buffer_1
endmodule
