// Logisim project Test.circ as structural Verilog: 8 circuits, main circuit main
module main (
  input  in_1,
  input  [7:0] inFromCdM8,
  input  in_3,
  input  in_4,
  input  [3:0] in_5,
  input  in_6,
  output [19:0] out_7,
  output [19:0] out_8,
  output [19:0] out_9,
  output [19:0] out_10,
  output [19:0] out_11,
  output [19:0] out_12,
  output [19:0] out_13,
  output [19:0] out_14,
  output [19:0] out_15,
  output [19:0] out_16,
  output [7:0] Frd,
  output [7:0] Snd,
  output [7:0] Fst,
  output CdM8,
  output out_21,
  output [15:0] out_22
);

  wire controlled_buffer_2_out, controlled_buffer_3_out, controlled_buffer_5_out, counter_1_carry,
       die_1_out_17, not_1_out, not_2_out, or_9_out, or_10_out, player_1_boom, pull_resistor_4_node,
       register_1_q, register_2_q, Reset, space;
  wire [2:0] random_1_out;
  wire [7:0] Input_0xF3, Input_0xF4, Input_0xF5;
  wire [15:0] counter_3_q;
  wire [19:0] he_1_out_15, he_1_out_16, he_1_out_17, he_1_out_18, he_1_out_19, he_1_out_20, he_1_out_21,
       he_1_out_22, he_1_out_23, he_1_out_24, or_1_out_3, or_2_out_3, or_3_out_3, or_4_out_3, or_5_out_3,
       or_6_out_3, or_7_out_3, or_8_out_3, player_1_out_16, player_1_out_17, player_1_out_18,
       player_1_out_19, player_1_out_20, player_1_out_21, player_1_out_22, player_1_out_23, player_1_out_24,
       player_1_out_25, player_1_out_27, player_1_out_28, player_1_out_29, player_1_out_30, player_1_out_31,
       player_1_out_32, player_1_out_33, player_1_out_34, player_1_out_35, player_1_out_36, shoot_1_out_4,
       shoot_1_out_5, shoot_1_out_6, shoot_1_out_7, shoot_1_out_8, shoot_1_out_9, shoot_1_out_10,
       shoot_1_out_11;

  assign space = in_1 ? in_4 : 1'bz;  // Controlled_Buffer controlled_buffer_1
  // Probe on inFromCdM8
  Counter #(.max('hc0)) counter_1 (
    .carry(counter_1_carry), .clk(controlled_buffer_2_out));  // open: load, D, count, Q, clr
  assign controlled_buffer_2_out = not_2_out ? controlled_buffer_3_out : 1'bz;  // Controlled_Buffer controlled_buffer_2
  assign controlled_buffer_3_out = in_1 ? in_6 : 1'bz;  // Controlled_Buffer controlled_buffer_3
  assign CdM8 = in_1 ? Reset : 1'bz;  // Controlled_Buffer controlled_buffer_4
  Counter #(.width(5), .max('h1f)) counter_2 (
    .carry(Reset), .clk(controlled_buffer_5_out));  // open: load, D, count, Q, clr
  assign controlled_buffer_5_out = not_1_out ? counter_1_carry : 1'bz;  // Controlled_Buffer controlled_buffer_5
  not not_1 (not_1_out, register_1_q);
  Register #(.width(1)) register_1 (.D(not_1_out), .Q(register_1_q), .clk(Reset), .clr(inFromCdM8[6]));  // open: en
  assign out_7 = in_1 ? player_1_out_16 : 20'bz;  // Controlled_Buffer controlled_buffer_6
  Random #(.width(3)) random_1 (.clk(Reset), .out(random_1_out));  // open: next, clr
  player player_1 (
    .Left(in_5[2]), .Right(in_5[1]), .out_16(player_1_out_16), .in_4(he_1_out_15), .in_5(he_1_out_16),
    .in_6(he_1_out_17), .in_7(he_1_out_18), .in_8(he_1_out_19), .in_9(he_1_out_20), .in_10(he_1_out_21),
    .in_11(he_1_out_22), .in_12(he_1_out_23), .in_13(he_1_out_24), .boom(player_1_boom), .Space(space),
    .Tic(counter_1_carry), .out_27(player_1_out_27), .takt(Reset), .out_29(player_1_out_29),
    .out_31(player_1_out_31), .out_33(player_1_out_33), .out_35(player_1_out_35), .out_28(player_1_out_28),
    .out_30(player_1_out_30), .out_32(player_1_out_32), .out_34(player_1_out_34), .out_36(player_1_out_36),
    .out_17(player_1_out_17), .out_18(player_1_out_18), .out_19(player_1_out_19), .out_20(player_1_out_20),
    .out_21(player_1_out_21), .out_22(player_1_out_22), .out_23(player_1_out_23), .out_24(player_1_out_24),
    .out_25(player_1_out_25));
  assign out_8 = in_1 ? or_1_out_3 : 20'bz;  // Controlled_Buffer controlled_buffer_7
  assign out_11 = in_1 ? or_4_out_3 : 20'bz;  // Controlled_Buffer controlled_buffer_8
  assign out_10 = in_1 ? or_2_out_3 : 20'bz;  // Controlled_Buffer controlled_buffer_9
  assign out_9 = in_1 ? or_3_out_3 : 20'bz;  // Controlled_Buffer controlled_buffer_10
  \or  or_1 (.in_1(shoot_1_out_4), .in_2(player_1_out_17), .out_3(or_1_out_3));
  \or  or_2 (.in_1(shoot_1_out_8), .in_2(player_1_out_19), .out_3(or_2_out_3));
  \or  or_3 (.in_1(shoot_1_out_6), .in_2(player_1_out_18), .out_3(or_3_out_3));
  \or  or_4 (.in_1(shoot_1_out_10), .in_2(player_1_out_20), .out_3(or_4_out_3));
  assign out_14 = in_1 ? or_6_out_3 : 20'bz;  // Controlled_Buffer controlled_buffer_11
  assign out_15 = in_1 ? or_7_out_3 : 20'bz;  // Controlled_Buffer controlled_buffer_12
  assign out_12 = in_1 ? or_5_out_3 : 20'bz;  // Controlled_Buffer controlled_buffer_13
  assign out_13 = in_1 ? or_8_out_3 : 20'bz;  // Controlled_Buffer controlled_buffer_14
  \or  or_5 (.in_1(shoot_1_out_5), .in_2(player_1_out_21), .out_3(or_5_out_3));
  \or  or_6 (.in_1(shoot_1_out_9), .in_2(player_1_out_23), .out_3(or_6_out_3));
  \or  or_7 (.in_1(shoot_1_out_11), .in_2(player_1_out_24), .out_3(or_7_out_3));
  \or  or_8 (.in_1(shoot_1_out_7), .in_2(player_1_out_22), .out_3(or_8_out_3));
  die die_1 (
    .in_1(shoot_1_out_4), .in_9(player_1_out_17), .in_2(shoot_1_out_6), .in_10(player_1_out_18),
    .in_3(shoot_1_out_8), .in_11(player_1_out_19), .in_4(shoot_1_out_10), .in_12(player_1_out_20),
    .in_5(shoot_1_out_5), .in_13(player_1_out_21), .in_6(shoot_1_out_7), .in_14(player_1_out_22),
    .in_7(shoot_1_out_9), .in_15(player_1_out_23), .in_8(shoot_1_out_11), .in_16(player_1_out_24),
    .out_17(die_1_out_17));
  assign out_16 = in_1 ? player_1_out_25 : 20'bz;  // Controlled_Buffer controlled_buffer_15
  shoot shoot_1 (
    .in_1(counter_1_carry), .in_3(inFromCdM8), .in_2(random_1_out), .out_4(shoot_1_out_4),
    .out_6(shoot_1_out_6), .out_8(shoot_1_out_8), .out_10(shoot_1_out_10), .out_5(shoot_1_out_5),
    .out_7(shoot_1_out_7), .out_9(shoot_1_out_9), .out_11(shoot_1_out_11));
  He he_1 (
    .Tic(Reset), .out_15(he_1_out_15), .out_16(he_1_out_16), .out_17(he_1_out_17), .out_18(he_1_out_18),
    .out_19(he_1_out_19), .out_20(he_1_out_20), .out_21(he_1_out_21), .out_22(he_1_out_22),
    .out_23(he_1_out_23), .out_24(he_1_out_24), .space(space), .in_6(counter_1_carry),
    .in_2(player_1_out_27), .in_4(player_1_out_29), .in_5(player_1_out_31), .in_7(player_1_out_33),
    .in_8(player_1_out_35), .in_9(player_1_out_28), .in_10(player_1_out_30), .in_11(player_1_out_32),
    .in_12(player_1_out_34), .in_13(player_1_out_36), .in_14(register_2_q));
  Multiplexer #(.select(3), .width(20), .enable("false")) multiplexer_1 (
    .in0(player_1_out_17), .in1(player_1_out_18), .in2(player_1_out_19), .in3(player_1_out_20),
    .in4(player_1_out_21), .in5(player_1_out_22), .in6(player_1_out_23), .in7(player_1_out_24),
    .out({Input_0xF5[3:0], Input_0xF4, Input_0xF3}), .sel(random_1_out));
  assign out_22 = in_1 ? counter_3_q : 16'bz;  // Controlled_Buffer controlled_buffer_16
  Counter #(.width(16), .max('hffff)) counter_3 (
    .Q(counter_3_q), .clk(Reset), .clr(or_9_out));  // open: load, D, count, carry
  or or_9 (or_9_out, die_1_out_17, player_1_boom);
  assign Frd = in_1 ? Input_0xF5 : 8'bz;  // Controlled_Buffer controlled_buffer_17
  Pull_Resistor pull_resistor_1 (.node(Input_0xF5));
  assign Snd = in_1 ? Input_0xF4 : 8'bz;  // Controlled_Buffer controlled_buffer_18
  Pull_Resistor pull_resistor_2 (.node(Input_0xF4));
  assign Fst = in_1 ? Input_0xF3 : 8'bz;  // Controlled_Buffer controlled_buffer_19
  Pull_Resistor pull_resistor_3 (.node(Input_0xF3));
  Pull_Resistor pull_resistor_4 (.node(pull_resistor_4_node));
  assign pull_resistor_4_node = in_1 ? in_3 : 1'bz;  // Controlled_Buffer controlled_buffer_20
  not not_2 (not_2_out, register_2_q);
  or or_10 (or_10_out, or_9_out, pull_resistor_4_node);
  assign out_21 = in_1 ? register_2_q : 1'bz;  // Controlled_Buffer controlled_buffer_21
  Register #(.width(1)) register_2 (.D(not_2_out), .Q(register_2_q), .clk(or_10_out), .clr(space));  // open: en

  // Other names for the same wires on the sheet: sel = in_1

  // Notes on the sheet:
  //   Left
  //   Right
  //   Space
endmodule

module He (
  input  Tic,
  input  [19:0] in_2,
  input  space,
  input  [19:0] in_4,
  input  [19:0] in_5,
  input  in_6,
  input  [19:0] in_7,
  input  [19:0] in_8,
  input  [19:0] in_9,
  input  [19:0] in_10,
  input  [19:0] in_11,
  input  [19:0] in_12,
  input  [19:0] in_13,
  input  in_14,
  output [19:0] out_15,
  output [19:0] out_16,
  output [19:0] out_17,
  output [19:0] out_18,
  output [19:0] out_19,
  output [19:0] out_20,
  output [19:0] out_21,
  output [19:0] out_22,
  output [19:0] out_23,
  output [19:0] out_24
);

  wire _0, _1, _2, _3, _4, _5, _6, _7, not_1_out, not_2_out, register_2_q, secret, Start, Takt;
  wire [19:0] and_2_out, and_3_out, and_4_out, and_5_out, and_6_out, and_7_out, and_8_out, and_9_out,
       and_10_out, and_11_out, multiplexer_1_out, multiplexer_2_out, multiplexer_3_out, multiplexer_4_out,
       multiplexer_5_out, multiplexer_6_out, multiplexer_7_out, multiplexer_8_out, multiplexer_9_out,
       multiplexer_10_out, or_1_out, or_2_out, or_3_out, or_4_out, or_5_out, or_6_out, or_7_out, or_8_out,
       or_9_out, or_10_out, pull_resistor_1_node, pull_resistor_2_node, pull_resistor_3_node,
       pull_resistor_4_node, pull_resistor_5_node, pull_resistor_6_node, pull_resistor_7_node,
       pull_resistor_8_node, pull_resistor_9_node, pull_resistor_10_node, register_3_q, register_4_q,
       register_5_q, register_6_q, register_7_q, register_8_q, register_9_q, register_10_q, register_11_q,
       register_12_q, shifter_1_out, shifter_2_out, shifter_3_out, shifter_4_out, shifter_5_out,
       shifter_6_out, shifter_7_out, shifter_8_out, shifter_9_out, shifter_10_out, shifter_11_out,
       shifter_12_out, shifter_13_out, shifter_14_out, shifter_15_out, shifter_16_out, shifter_17_out,
       shifter_18_out, shifter_19_out, shifter_20_out;

  not not_1 (not_1_out, secret);
  Register #(.width(1)) register_1 (.D(not_1_out), .en(not_1_out), .Q(secret), .clk(space));  // open: clr
  not not_2 (not_2_out, Tic);
  and and_1 (Takt, not_2_out, Tic);
  Random random_1 (.clk(Takt), .out({_0, _1, _2, _3, _4, _5, _6, _7}));  // open: next, clr
  Multiplexer #(.width(20), .enable("false")) multiplexer_1 (
    .in0(register_3_q), .in1(20'h701e), .out(multiplexer_1_out), .sel(Start));
  Multiplexer #(.width(20), .enable("false")) multiplexer_2 (
    .in0(register_4_q), .in1(20'h8fb4), .out(multiplexer_2_out), .sel(Start));
  Multiplexer #(.width(20), .enable("false")) multiplexer_3 (
    .in0(register_5_q), .in1(20'h1607e), .out(multiplexer_3_out), .sel(Start));
  Multiplexer #(.width(20), .enable("false")) multiplexer_4 (
    .in0(register_6_q), .in1(20'h9377), .out(multiplexer_4_out), .sel(Start));
  Multiplexer #(.width(20), .enable("false")) multiplexer_5 (
    .in0(register_7_q), .in1(20'h86c), .out(multiplexer_5_out), .sel(Start));
  Multiplexer #(.width(20), .enable("false")) multiplexer_6 (
    .in0(register_8_q), .in1(20'h854), .out(multiplexer_6_out), .sel(Start));
  Multiplexer #(.width(20), .enable("false")) multiplexer_7 (
    .in0(register_9_q), .in1(20'h936f), .out(multiplexer_7_out), .sel(Start));
  Multiplexer #(.width(20), .enable("false")) multiplexer_8 (
    .in0(register_10_q), .in1(20'h1607e), .out(multiplexer_8_out), .sel(Start));
  Multiplexer #(.width(20), .enable("false")) multiplexer_9 (
    .in0(register_11_q), .in1(20'h8f9c), .out(multiplexer_9_out), .sel(Start));
  Multiplexer #(.width(20), .enable("false")) multiplexer_10 (
    .in0(register_12_q), .in1(20'h7000), .out(multiplexer_10_out), .sel(Start));
  not not_3 (Start, register_2_q);
  Register #(.width(1)) register_2 (.D(Start), .en(Start), .Q(register_2_q), .clk(Takt));  // open: clr
  Shifter #(.width(20), .shift("lr")) shifter_1 (.in(multiplexer_1_out), .\dist (5'b00001), .out(shifter_1_out));
  Register #(.width(20)) register_3 (.D(shifter_1_out), .Q(register_3_q), .clk(Takt));  // open: en, clr
  Register #(.width(20)) register_4 (.D(shifter_2_out), .Q(register_4_q), .clk(Takt));  // open: en, clr
  Shifter #(.width(20), .shift("lr")) shifter_2 (.in(multiplexer_2_out), .\dist (5'b00001), .out(shifter_2_out));
  Shifter #(.width(20), .shift("lr")) shifter_3 (.in(multiplexer_3_out), .\dist (5'b00001), .out(shifter_3_out));
  Register #(.width(20)) register_5 (.D(shifter_3_out), .Q(register_5_q), .clk(Takt));  // open: en, clr
  Shifter #(.width(20), .shift("lr")) shifter_4 (.in(multiplexer_4_out), .\dist (5'b00001), .out(shifter_4_out));
  Register #(.width(20)) register_6 (.D(shifter_4_out), .Q(register_6_q), .clk(Takt));  // open: en, clr
  Register #(.width(20)) register_7 (.D(shifter_5_out), .Q(register_7_q), .clk(Takt));  // open: en, clr
  Shifter #(.width(20), .shift("lr")) shifter_5 (.in(multiplexer_5_out), .\dist (5'b00001), .out(shifter_5_out));
  Shifter #(.width(20), .shift("lr")) shifter_6 (.in(multiplexer_6_out), .\dist (5'b00001), .out(shifter_6_out));
  Register #(.width(20)) register_8 (.D(shifter_6_out), .Q(register_8_q), .clk(Takt));  // open: en, clr
  Shifter #(.width(20), .shift("lr")) shifter_7 (.in(multiplexer_7_out), .\dist (5'b00001), .out(shifter_7_out));
  Register #(.width(20)) register_9 (.D(shifter_7_out), .Q(register_9_q), .clk(Takt));  // open: en, clr
  Register #(.width(20)) register_10 (.D(shifter_8_out), .Q(register_10_q), .clk(Takt));  // open: en, clr
  Shifter #(.width(20), .shift("lr")) shifter_8 (.in(multiplexer_8_out), .\dist (5'b00001), .out(shifter_8_out));
  Register #(.width(20)) register_11 (.D(shifter_9_out), .Q(register_11_q), .clk(Takt));  // open: en, clr
  Shifter #(.width(20), .shift("lr")) shifter_9 (.in(multiplexer_9_out), .\dist (5'b00001), .out(shifter_9_out));
  Register #(.width(20)) register_12 (.D(shifter_10_out), .Q(register_12_q), .clk(Takt));  // open: en, clr
  Shifter #(.width(20), .shift("lr")) shifter_10 (.in(multiplexer_10_out), .\dist (5'b00001), .out(shifter_10_out));
  Multiplexer #(.disabled(0), .enable("false")) multiplexer_11 (
    .in0(multiplexer_1_out[0]), .in1(1'b0), .out(pull_resistor_1_node[19]), .sel(secret));
  Multiplexer #(.disabled(0), .enable("false")) multiplexer_12 (
    .in0(multiplexer_2_out[0]), .in1(_7), .out(pull_resistor_2_node[19]), .sel(secret));
  Multiplexer #(.disabled(0), .enable("false")) multiplexer_13 (
    .in0(multiplexer_3_out[0]), .in1(_6), .out(pull_resistor_3_node[19]), .sel(secret));
  Multiplexer #(.disabled(0), .enable("false")) multiplexer_14 (
    .in0(multiplexer_4_out[0]), .in1(_5), .out(pull_resistor_4_node[19]), .sel(secret));
  Multiplexer #(.disabled(0), .enable("false")) multiplexer_15 (
    .in0(multiplexer_5_out[0]), .in1(_4), .out(pull_resistor_5_node[19]), .sel(secret));
  Multiplexer #(.disabled(0), .enable("false")) multiplexer_16 (
    .in0(multiplexer_6_out[0]), .in1(_3), .out(pull_resistor_6_node[19]), .sel(secret));
  Multiplexer #(.disabled(0), .enable("false")) multiplexer_17 (
    .in0(multiplexer_7_out[0]), .in1(_2), .out(pull_resistor_7_node[19]), .sel(secret));
  Multiplexer #(.disabled(0), .enable("false")) multiplexer_18 (
    .in0(multiplexer_8_out[0]), .in1(_1), .out(pull_resistor_8_node[19]), .sel(secret));
  Multiplexer #(.disabled(0), .enable("false")) multiplexer_19 (
    .in0(multiplexer_9_out[0]), .in1(_0), .out(pull_resistor_9_node[19]), .sel(secret));
  Multiplexer #(.disabled(0), .enable("false")) multiplexer_20 (
    .in0(multiplexer_10_out[0]), .in1(1'b0), .out(pull_resistor_10_node[19]), .sel(secret));
  Pull_Resistor pull_resistor_1 (.node(pull_resistor_1_node));
  Shifter #(.width(20), .shift("lr")) shifter_11 (.in(and_2_out), .\dist (5'b00001), .out(shifter_11_out));
  Pull_Resistor pull_resistor_2 (.node(pull_resistor_2_node));
  Shifter #(.width(20), .shift("lr")) shifter_12 (.in(and_3_out), .\dist (5'b00001), .out(shifter_12_out));
  Pull_Resistor pull_resistor_3 (.node(pull_resistor_3_node));
  Shifter #(.width(20), .shift("lr")) shifter_13 (.in(and_4_out), .\dist (5'b00001), .out(shifter_13_out));
  Pull_Resistor pull_resistor_4 (.node(pull_resistor_4_node));
  Shifter #(.width(20), .shift("lr")) shifter_14 (.in(and_5_out), .\dist (5'b00001), .out(shifter_14_out));
  Pull_Resistor pull_resistor_5 (.node(pull_resistor_5_node));
  Shifter #(.width(20), .shift("lr")) shifter_15 (.in(and_6_out), .\dist (5'b00001), .out(shifter_15_out));
  Pull_Resistor pull_resistor_6 (.node(pull_resistor_6_node));
  Shifter #(.width(20), .shift("lr")) shifter_16 (.in(and_7_out), .\dist (5'b00001), .out(shifter_16_out));
  Pull_Resistor pull_resistor_7 (.node(pull_resistor_7_node));
  Shifter #(.width(20), .shift("lr")) shifter_17 (.in(and_8_out), .\dist (5'b00001), .out(shifter_17_out));
  Pull_Resistor pull_resistor_8 (.node(pull_resistor_8_node));
  Shifter #(.width(20), .shift("lr")) shifter_18 (.in(and_9_out), .\dist (5'b00001), .out(shifter_18_out));
  Pull_Resistor pull_resistor_9 (.node(pull_resistor_9_node));
  Shifter #(.width(20), .shift("lr")) shifter_19 (.in(and_10_out), .\dist (5'b00001), .out(shifter_19_out));
  Pull_Resistor pull_resistor_10 (.node(pull_resistor_10_node));
  Shifter #(.width(20), .shift("lr")) shifter_20 (.in(and_11_out), .\dist (5'b00001), .out(shifter_20_out));
  assign and_2_out = out_15 & in_2;  // AND_Gate and_2, 20 bits wide
  Register #(.width(20)) register_13 (.D(or_1_out), .Q(out_15), .clk(Takt), .clr(in_14));  // open: en
  assign or_1_out = pull_resistor_1_node | shifter_11_out;  // OR_Gate or_1, 20 bits wide
  assign and_3_out = out_16 & in_4;  // AND_Gate and_3, 20 bits wide
  assign or_2_out = pull_resistor_2_node | shifter_12_out;  // OR_Gate or_2, 20 bits wide
  Register #(.width(20)) register_14 (.D(or_2_out), .Q(out_16), .clk(Takt), .clr(in_14));  // open: en
  assign and_4_out = out_17 & in_5;  // AND_Gate and_4, 20 bits wide
  Register #(.width(20)) register_15 (.D(or_3_out), .Q(out_17), .clk(Takt), .clr(in_14));  // open: en
  assign or_3_out = pull_resistor_3_node | shifter_13_out;  // OR_Gate or_3, 20 bits wide
  assign and_5_out = out_18 & in_7;  // AND_Gate and_5, 20 bits wide
  Register #(.width(20)) register_16 (.D(or_4_out), .Q(out_18), .clk(Takt), .clr(in_14));  // open: en
  assign or_4_out = pull_resistor_4_node | shifter_14_out;  // OR_Gate or_4, 20 bits wide
  assign and_6_out = out_19 & in_8;  // AND_Gate and_6, 20 bits wide
  Register #(.width(20)) register_17 (.D(or_5_out), .Q(out_19), .clk(Takt), .clr(in_14));  // open: en
  assign or_5_out = pull_resistor_5_node | shifter_15_out;  // OR_Gate or_5, 20 bits wide
  assign and_7_out = out_20 & in_9;  // AND_Gate and_7, 20 bits wide
  assign or_6_out = pull_resistor_6_node | shifter_16_out;  // OR_Gate or_6, 20 bits wide
  Register #(.width(20)) register_18 (.D(or_6_out), .Q(out_20), .clk(Takt), .clr(in_14));  // open: en
  assign and_8_out = out_21 & in_10;  // AND_Gate and_8, 20 bits wide
  Register #(.width(20)) register_19 (.D(or_7_out), .Q(out_21), .clk(Takt), .clr(in_14));  // open: en
  assign or_7_out = pull_resistor_7_node | shifter_17_out;  // OR_Gate or_7, 20 bits wide
  assign and_9_out = out_22 & in_11;  // AND_Gate and_9, 20 bits wide
  Register #(.width(20)) register_20 (.D(or_8_out), .Q(out_22), .clk(Takt), .clr(in_14));  // open: en
  assign or_8_out = pull_resistor_8_node | shifter_18_out;  // OR_Gate or_8, 20 bits wide
  assign and_10_out = out_23 & in_12;  // AND_Gate and_10, 20 bits wide
  Register #(.width(20)) register_21 (.D(or_9_out), .Q(out_23), .clk(Takt), .clr(in_14));  // open: en
  assign or_9_out = pull_resistor_9_node | shifter_19_out;  // OR_Gate or_9, 20 bits wide
  assign and_11_out = out_24 & in_13;  // AND_Gate and_11, 20 bits wide
  assign or_10_out = pull_resistor_10_node | shifter_20_out;  // OR_Gate or_10, 20 bits wide
  Register #(.width(20)) register_22 (.D(or_10_out), .Q(out_24), .clk(Takt), .clr(in_14));  // open: en

  // Other names for the same wires on the sheet: Tic_t = in_6
endmodule

module player (
  input  Left,
  input  Right,
  input  Space,
  input  [19:0] in_4,
  input  [19:0] in_5,
  input  [19:0] in_6,
  input  [19:0] in_7,
  input  [19:0] in_8,
  input  [19:0] in_9,
  input  [19:0] in_10,
  input  [19:0] in_11,
  input  [19:0] in_12,
  input  [19:0] in_13,
  input  Tic,
  input  takt,
  output [19:0] out_16,
  output [19:0] out_17,
  output [19:0] out_18,
  output [19:0] out_19,
  output [19:0] out_20,
  output [19:0] out_21,
  output [19:0] out_22,
  output [19:0] out_23,
  output [19:0] out_24,
  output [19:0] out_25,
  output boom,
  output [19:0] out_27,
  output [19:0] out_28,
  output [19:0] out_29,
  output [19:0] out_30,
  output [19:0] out_31,
  output [19:0] out_32,
  output [19:0] out_33,
  output [19:0] out_34,
  output [19:0] out_35,
  output [19:0] out_36
);

  wire _0, _1, _2, _3, _4, _5, _6, _7, _8, _9, not_1_out, not_2_out, or_1_out, or_32_out, register_1_q,
       Space_t, Takt_t;
  wire [3:0] counter_1_q;
  wire [19:0] A0, A1, A2, A3, A4, A5, A6, A7, A8, A9, and_5_out, and_6_out, and_7_out, and_8_out, and_9_out,
       and_10_out, and_11_out, and_12_out, and_13_out, and_14_out, and_20_out, and_21_out, and_22_out,
       and_23_out, and_24_out, and_25_out, and_26_out, and_27_out, and_28_out, and_29_out, or_2_out,
       or_3_out, or_4_out, or_5_out, or_6_out, or_7_out, or_8_out, or_9_out, or_10_out, or_11_out, or_12_out,
       or_13_out, or_14_out, or_15_out, or_16_out, or_17_out, or_18_out, or_19_out, or_20_out, or_21_out,
       or_22_out, or_23_out, or_24_out, or_25_out, or_26_out, or_27_out, or_28_out, or_29_out, or_30_out,
       or_31_out, pull_resistor_2_node, pull_resistor_4_node, pull_resistor_6_node, pull_resistor_13_node,
       pull_resistor_15_node, pull_resistor_17_node, pull_resistor_19_node, pull_resistor_21_node,
       pull_resistor_28_node, pull_resistor_30_node, shifter_1_out, shifter_2_out, shifter_3_out,
       shifter_4_out, shifter_5_out, shifter_6_out, shifter_7_out, shifter_8_out, shifter_9_out,
       shifter_10_out;
  wire [19:1] pull_resistor_1_node, pull_resistor_3_node, pull_resistor_5_node, pull_resistor_12_node,
       pull_resistor_14_node, pull_resistor_16_node, pull_resistor_18_node, pull_resistor_20_node,
       pull_resistor_27_node, pull_resistor_29_node;

  or or_1 (or_1_out, Right, Left);
  Register #(.width(1)) register_1 (.D(Space), .Q(register_1_q), .clk(Space), .clr(Space_t));  // open: en
  not not_1 (not_1_out, takt);
  and and_1 (Takt_t, not_1_out, takt);
  mask mask_1 (.in_2(A0), .in_3(in_4), .out_4(out_27), .in_1(Takt_t));
  mask mask_2 (.in_2(A1), .in_3(in_5), .out_4(out_29), .in_1(Takt_t));
  mask mask_3 (.in_2(A2), .in_3(in_6), .out_4(out_31), .in_1(Takt_t));
  mask mask_4 (.in_2(A3), .in_3(in_7), .out_4(out_33), .in_1(Takt_t));
  mask mask_5 (.in_2(A4), .in_3(in_8), .out_4(out_35), .in_1(Takt_t));
  Decoder #(.select(4), .disabled(0), .enable("false")) decoder_1 (
    .out0(_0), .out1(_1), .out2(_2), .out3(_3), .out4(_4), .out5(_5), .out6(_6), .out7(_7), .out8(_8),
    .out9(_9), .sel(counter_1_q));  // open: out10, out11, out12, out13, out14, out15
  Counter #(.width(4), .max('h9)) counter_1 (
    .load(Left), .Q(counter_1_q), .clk(or_1_out));  // open: D, count, carry, clr
  D_Flip_Flop d_ff_1 (.clk(Tic), .D(register_1_q), .Q(Space_t), .preset(register_1_q));  // open: Qn, en, reset
  mask mask_6 (.in_2(A5), .in_3(in_9), .out_4(out_28), .in_1(Takt_t));
  mask mask_7 (.in_2(A6), .in_3(in_10), .out_4(out_30), .in_1(Takt_t));
  mask mask_8 (.in_2(A7), .in_3(in_11), .out_4(out_32), .in_1(Takt_t));
  mask mask_9 (.in_2(A8), .in_3(in_12), .out_4(out_34), .in_1(Takt_t));
  mask mask_10 (.in_2(A9), .in_3(in_13), .out_4(out_36), .in_1(Takt_t));
  assign out_16 = out_27 & or_2_out;  // AND_Gate and_2, 20 bits wide
  assign or_2_out = A0 | or_3_out;  // OR_Gate or_2, 20 bits wide
  assign or_3_out = {pull_resistor_1_node, _0} | pull_resistor_2_node;  // OR_Gate or_3, 20 bits wide
  Pull_Resistor pull_resistor_1 (.node({pull_resistor_1_node, _0}));
  Pull_Resistor pull_resistor_2 (.node(pull_resistor_2_node));
  assign pull_resistor_2_node = not_2_out ? in_4 : 20'bz;  // Controlled_Buffer controlled_buffer_1
  assign out_17 = out_29 & or_4_out;  // AND_Gate and_3, 20 bits wide
  assign or_4_out = A1 | or_5_out;  // OR_Gate or_4, 20 bits wide
  assign or_5_out = {pull_resistor_3_node, _1} | pull_resistor_4_node;  // OR_Gate or_5, 20 bits wide
  Pull_Resistor pull_resistor_3 (.node({pull_resistor_3_node, _1}));
  Pull_Resistor pull_resistor_4 (.node(pull_resistor_4_node));
  assign pull_resistor_4_node = not_2_out ? in_5 : 20'bz;  // Controlled_Buffer controlled_buffer_2
  assign out_18 = out_31 & or_6_out;  // AND_Gate and_4, 20 bits wide
  assign or_6_out = A2 | or_7_out;  // OR_Gate or_6, 20 bits wide
  assign or_7_out = {pull_resistor_5_node, _2} | pull_resistor_6_node;  // OR_Gate or_7, 20 bits wide
  Pull_Resistor pull_resistor_5 (.node({pull_resistor_5_node, _2}));
  Pull_Resistor pull_resistor_6 (.node(pull_resistor_6_node));
  assign pull_resistor_6_node = not_2_out ? in_6 : 20'bz;  // Controlled_Buffer controlled_buffer_3
  and and_5 (and_5_out[0], Space_t, _0);
  Pull_Resistor pull_resistor_7 (.node(and_5_out));
  assign and_6_out = A0 & out_27;  // AND_Gate and_6, 20 bits wide
  and and_7 (and_7_out[0], Space_t, _1);
  Pull_Resistor pull_resistor_8 (.node(and_7_out));
  assign and_8_out = A1 & out_29;  // AND_Gate and_8, 20 bits wide
  and and_9 (and_9_out[0], Space_t, _2);
  Pull_Resistor pull_resistor_9 (.node(and_9_out));
  assign and_10_out = A2 & out_31;  // AND_Gate and_10, 20 bits wide
  and and_11 (and_11_out[0], Space_t, _3);
  Pull_Resistor pull_resistor_10 (.node(and_11_out));
  assign and_12_out = A3 & out_33;  // AND_Gate and_12, 20 bits wide
  and and_13 (and_13_out[0], Space_t, _4);
  Pull_Resistor pull_resistor_11 (.node(and_13_out));
  assign and_14_out = A4 & out_35;  // AND_Gate and_14, 20 bits wide
  assign out_19 = out_33 & or_8_out;  // AND_Gate and_15, 20 bits wide
  assign or_8_out = A3 | or_9_out;  // OR_Gate or_8, 20 bits wide
  assign or_9_out = {pull_resistor_12_node, _3} | pull_resistor_13_node;  // OR_Gate or_9, 20 bits wide
  Pull_Resistor pull_resistor_12 (.node({pull_resistor_12_node, _3}));
  Pull_Resistor pull_resistor_13 (.node(pull_resistor_13_node));
  assign pull_resistor_13_node = not_2_out ? in_7 : 20'bz;  // Controlled_Buffer controlled_buffer_4
  assign or_10_out = and_5_out | and_6_out;  // OR_Gate or_10, 20 bits wide
  Shifter #(.width(20)) shifter_1 (.in(or_10_out), .\dist (5'b00001), .out(shifter_1_out));
  assign or_11_out = and_7_out | and_8_out;  // OR_Gate or_11, 20 bits wide
  Shifter #(.width(20)) shifter_2 (.in(or_11_out), .\dist (5'b00001), .out(shifter_2_out));
  assign or_12_out = and_9_out | and_10_out;  // OR_Gate or_12, 20 bits wide
  Shifter #(.width(20)) shifter_3 (.in(or_12_out), .\dist (5'b00001), .out(shifter_3_out));
  assign or_13_out = and_11_out | and_12_out;  // OR_Gate or_13, 20 bits wide
  Shifter #(.width(20)) shifter_4 (.in(or_13_out), .\dist (5'b00001), .out(shifter_4_out));
  assign or_14_out = and_13_out | and_14_out;  // OR_Gate or_14, 20 bits wide
  Shifter #(.width(20)) shifter_5 (.in(or_14_out), .\dist (5'b00001), .out(shifter_5_out));
  assign out_20 = out_35 & or_15_out;  // AND_Gate and_16, 20 bits wide
  assign or_15_out = A4 | or_16_out;  // OR_Gate or_15, 20 bits wide
  assign or_16_out = {pull_resistor_14_node, _4} | pull_resistor_15_node;  // OR_Gate or_16, 20 bits wide
  Pull_Resistor pull_resistor_14 (.node({pull_resistor_14_node, _4}));
  Pull_Resistor pull_resistor_15 (.node(pull_resistor_15_node));
  assign pull_resistor_15_node = not_2_out ? in_8 : 20'bz;  // Controlled_Buffer controlled_buffer_5
  Register #(.width(20)) register_2 (.D(shifter_1_out), .Q(A0), .clk(Tic));  // open: en, clr
  Register #(.width(20)) register_3 (.D(shifter_2_out), .Q(A1), .clk(Tic));  // open: en, clr
  Register #(.width(20)) register_4 (.D(shifter_3_out), .Q(A2), .clk(Tic));  // open: en, clr
  Register #(.width(20)) register_5 (.D(shifter_4_out), .Q(A3), .clk(Tic));  // open: en, clr
  Register #(.width(20)) register_6 (.D(shifter_5_out), .Q(A4), .clk(Tic));  // open: en, clr
  assign out_21 = out_28 & or_17_out;  // AND_Gate and_17, 20 bits wide
  assign or_17_out = A5 | or_18_out;  // OR_Gate or_17, 20 bits wide
  assign or_18_out = {pull_resistor_16_node, _5} | pull_resistor_17_node;  // OR_Gate or_18, 20 bits wide
  Pull_Resistor pull_resistor_16 (.node({pull_resistor_16_node, _5}));
  Pull_Resistor pull_resistor_17 (.node(pull_resistor_17_node));
  assign pull_resistor_17_node = not_2_out ? in_9 : 20'bz;  // Controlled_Buffer controlled_buffer_6
  assign out_22 = out_30 & or_19_out;  // AND_Gate and_18, 20 bits wide
  assign or_19_out = A6 | or_20_out;  // OR_Gate or_19, 20 bits wide
  assign or_20_out = {pull_resistor_18_node, _6} | pull_resistor_19_node;  // OR_Gate or_20, 20 bits wide
  Pull_Resistor pull_resistor_18 (.node({pull_resistor_18_node, _6}));
  Pull_Resistor pull_resistor_19 (.node(pull_resistor_19_node));
  assign pull_resistor_19_node = not_2_out ? in_10 : 20'bz;  // Controlled_Buffer controlled_buffer_7
  assign out_23 = out_32 & or_21_out;  // AND_Gate and_19, 20 bits wide
  assign or_21_out = A7 | or_22_out;  // OR_Gate or_21, 20 bits wide
  assign or_22_out = {pull_resistor_20_node, _7} | pull_resistor_21_node;  // OR_Gate or_22, 20 bits wide
  Pull_Resistor pull_resistor_20 (.node({pull_resistor_20_node, _7}));
  Pull_Resistor pull_resistor_21 (.node(pull_resistor_21_node));
  assign pull_resistor_21_node = not_2_out ? in_11 : 20'bz;  // Controlled_Buffer controlled_buffer_8
  and and_20 (and_20_out[0], Space_t, _5);
  Pull_Resistor pull_resistor_22 (.node(and_20_out));
  assign and_21_out = A5 & out_28;  // AND_Gate and_21, 20 bits wide
  and and_22 (and_22_out[0], Space_t, _6);
  Pull_Resistor pull_resistor_23 (.node(and_22_out));
  assign and_23_out = A6 & out_30;  // AND_Gate and_23, 20 bits wide
  and and_24 (and_24_out[0], Space_t, _7);
  Pull_Resistor pull_resistor_24 (.node(and_24_out));
  assign and_25_out = A7 & out_32;  // AND_Gate and_25, 20 bits wide
  and and_26 (and_26_out[0], Space_t, _8);
  Pull_Resistor pull_resistor_25 (.node(and_26_out));
  assign and_27_out = A8 & out_34;  // AND_Gate and_27, 20 bits wide
  and and_28 (and_28_out[0], Space_t, _9);
  Pull_Resistor pull_resistor_26 (.node(and_28_out));
  assign and_29_out = A9 & out_36;  // AND_Gate and_29, 20 bits wide
  assign out_24 = out_34 & or_23_out;  // AND_Gate and_30, 20 bits wide
  assign or_23_out = A8 | or_24_out;  // OR_Gate or_23, 20 bits wide
  assign or_24_out = {pull_resistor_27_node, _8} | pull_resistor_28_node;  // OR_Gate or_24, 20 bits wide
  Pull_Resistor pull_resistor_27 (.node({pull_resistor_27_node, _8}));
  Pull_Resistor pull_resistor_28 (.node(pull_resistor_28_node));
  assign pull_resistor_28_node = not_2_out ? in_12 : 20'bz;  // Controlled_Buffer controlled_buffer_9
  assign or_25_out = and_20_out | and_21_out;  // OR_Gate or_25, 20 bits wide
  Shifter #(.width(20)) shifter_6 (.in(or_25_out), .\dist (5'b00001), .out(shifter_6_out));
  assign or_26_out = and_22_out | and_23_out;  // OR_Gate or_26, 20 bits wide
  Shifter #(.width(20)) shifter_7 (.in(or_26_out), .\dist (5'b00001), .out(shifter_7_out));
  assign or_27_out = and_24_out | and_25_out;  // OR_Gate or_27, 20 bits wide
  Shifter #(.width(20)) shifter_8 (.in(or_27_out), .\dist (5'b00001), .out(shifter_8_out));
  assign or_28_out = and_26_out | and_27_out;  // OR_Gate or_28, 20 bits wide
  Shifter #(.width(20)) shifter_9 (.in(or_28_out), .\dist (5'b00001), .out(shifter_9_out));
  assign or_29_out = and_28_out | and_29_out;  // OR_Gate or_29, 20 bits wide
  Shifter #(.width(20)) shifter_10 (.in(or_29_out), .\dist (5'b00001), .out(shifter_10_out));
  assign out_25 = out_36 & or_30_out;  // AND_Gate and_31, 20 bits wide
  assign or_30_out = A9 | or_31_out;  // OR_Gate or_30, 20 bits wide
  assign or_31_out = {pull_resistor_29_node, _9} | pull_resistor_30_node;  // OR_Gate or_31, 20 bits wide
  Pull_Resistor pull_resistor_29 (.node({pull_resistor_29_node, _9}));
  Pull_Resistor pull_resistor_30 (.node(pull_resistor_30_node));
  assign pull_resistor_30_node = not_2_out ? in_13 : 20'bz;  // Controlled_Buffer controlled_buffer_10
  Register #(.width(20)) register_7 (.D(shifter_6_out), .Q(A5), .clk(Tic));  // open: en, clr
  Register #(.width(20)) register_8 (.D(shifter_7_out), .Q(A6), .clk(Tic));  // open: en, clr
  Register #(.width(20)) register_9 (.D(shifter_8_out), .Q(A7), .clk(Tic));  // open: en, clr
  Register #(.width(20)) register_10 (.D(shifter_9_out), .Q(A8), .clk(Tic));  // open: en, clr
  Register #(.width(20)) register_11 (.D(shifter_10_out), .Q(A9), .clk(Tic));  // open: en, clr
  not not_2 (not_2_out, boom);
  Register #(.width(1)) register_12 (.D(or_32_out), .Q(boom), .clk(or_32_out));  // open: en, clr
  or or_32 (or_32_out, in_4[0], in_5[0], in_6[0], in_7[0], in_8[0], in_9[0], in_10[0], in_11[0], in_12[0], in_13[0]);

  // Other names for the same wires on the sheet: B0[19:0] = in_4; B1[19:0] = in_5; B2[19:0] = in_6; B3[19:0] = in_7;
  //   B4[19:0] = in_8; B5[19:0] = in_9; B6[19:0] = in_10; B7[19:0] = in_11; B8[19:0] = in_12; B9[19:0] = in_13;
  //   C0[19:0] = out_27; C1[19:0] = out_29; C2[19:0] = out_31; C3[19:0] = out_33; C4[19:0] = out_35;
  //   C5[19:0] = out_28; C6[19:0] = out_30; C7[19:0] = out_32; C8[19:0] = out_34; C9[19:0] = out_36
endmodule

module mask (
  input  in_1,
  input  [19:0] in_2,
  input  [19:0] in_3,
  output [19:0] out_4
);

  wire bitfinder_1_found, bitfinder_2_found, comparator_1_eq, controlled_buffer_1_out,
       controlled_buffer_2_out, d_ff_1_q;
  wire [4:0] bitfinder_1_index, bitfinder_2_index;
  wire [19:0] decoder_1_out0, multiplexer_1_out;

  BitFinder #(.width(20), .\type ("high1")) bitfinder_1 (
    .in(in_2), .index(bitfinder_1_index), .found(bitfinder_1_found));
  Comparator #(.width(5)) comparator_1 (
    .a(bitfinder_1_index), .b(bitfinder_2_index), .eq(comparator_1_eq));  // open: gt, lt
  BitFinder #(.width(20)) bitfinder_2 (.in(in_3), .index(bitfinder_2_index), .found(bitfinder_2_found));
  Decoder #(.select(5), .disabled(0)) decoder_1 (
    .out0(decoder_1_out0[0]), .out1(decoder_1_out0[1]), .out2(decoder_1_out0[2]), .out3(decoder_1_out0[3]),
    .out4(decoder_1_out0[4]), .out5(decoder_1_out0[5]), .out6(decoder_1_out0[6]), .out7(decoder_1_out0[7]),
    .out8(decoder_1_out0[8]), .out9(decoder_1_out0[9]), .out10(decoder_1_out0[10]),
    .out11(decoder_1_out0[11]), .out12(decoder_1_out0[12]), .out13(decoder_1_out0[13]),
    .out14(decoder_1_out0[14]), .out15(decoder_1_out0[15]), .out16(decoder_1_out0[16]),
    .out17(decoder_1_out0[17]), .out18(decoder_1_out0[18]), .out19(decoder_1_out0[19]),
    .sel(bitfinder_2_index));  // open: out20, out21, out22, out23, out24, out25, out26, out27, out28, out29, out30, out31, en
  assign controlled_buffer_1_out = bitfinder_2_found ? comparator_1_eq : 1'bz;  // Controlled_Buffer controlled_buffer_1
  assign controlled_buffer_2_out = bitfinder_1_found ? controlled_buffer_1_out : 1'bz;  // Controlled_Buffer controlled_buffer_2
  Pull_Resistor pull_resistor_1 (.node(controlled_buffer_2_out));
  D_Flip_Flop d_ff_1 (
    .D(controlled_buffer_2_out), .Q(d_ff_1_q), .preset(controlled_buffer_2_out), .reset(in_1));  // open: clk, Qn, en
  Multiplexer #(.width(20), .disabled(0), .enable("false")) multiplexer_1 (
    .in0({20{1'b0}}), .in1(decoder_1_out0), .out(multiplexer_1_out), .sel(d_ff_1_q));
  assign out_4 = ~multiplexer_1_out;  // NOT_Gate not_1, 20 bits wide
endmodule

module shoot (
  input  in_1,
  input  [2:0] in_2,
  input  [7:0] in_3,
  output [19:0] out_4,
  output [19:0] out_5,
  output [19:0] out_6,
  output [19:0] out_7,
  output [19:0] out_8,
  output [19:0] out_9,
  output [19:0] out_10,
  output [19:0] out_11
);

  wire _1, _2, _3, _4, _5, _6, _7, _8, d_ff_1_q, register_1_q;
  wire [4:0] register_2_q;
  wire [19:0] controlled_buffer_1_out, controlled_buffer_2_out, controlled_buffer_6_out, or_1_out, or_2_out,
       or_3_out, or_4_out, or_5_out, or_6_out, or_7_out, or_8_out, pull_resistor_3_node,
       pull_resistor_4_node, pull_resistor_5_node, pull_resistor_7_node, pull_resistor_8_node, shifter_1_out,
       shifter_2_out, shifter_3_out, shifter_4_out, shifter_5_out, shifter_6_out, shifter_7_out,
       shifter_8_out, shoot;

  Decoder #(.select(3), .disabled(0), .enable("false")) decoder_1 (
    .out0(_1), .out1(_2), .out2(_3), .out3(_4), .out4(_5), .out5(_6), .out6(_7), .out7(_8), .sel(in_2));
  Register #(.width(1)) register_1 (.D(in_3[6]), .Q(register_1_q), .clk(in_3[6]), .clr(d_ff_1_q));  // open: en
  D_Flip_Flop d_ff_1 (.clk(in_1), .D(register_1_q), .Q(d_ff_1_q), .preset(register_1_q));  // open: Qn, en, reset
  Decoder #(.select(5), .disabled(0)) decoder_2 (
    .out0(shoot[0]), .out1(shoot[1]), .out2(shoot[2]), .out3(shoot[3]), .out4(shoot[4]), .out5(shoot[5]),
    .out6(shoot[6]), .out7(shoot[7]), .out8(shoot[8]), .out9(shoot[9]), .out10(shoot[10]), .out11(shoot[11]),
    .out12(shoot[12]), .out13(shoot[13]), .out14(shoot[14]), .out15(shoot[15]), .out16(shoot[16]),
    .out17(shoot[17]), .out18(shoot[18]), .out19(shoot[19]), .sel(register_2_q), .en(d_ff_1_q));  // open: out20, out21, out22, out23, out24, out25, out26, out27, out28, out29, out30, out31
  Register #(.width(5)) register_2 (.D(in_3[4:0]), .Q(register_2_q), .clk(in_3[6]));  // open: en, clr
  assign controlled_buffer_1_out = _1 ? shoot : 20'bz;  // Controlled_Buffer controlled_buffer_1
  Pull_Resistor pull_resistor_1 (.node(controlled_buffer_1_out));
  assign controlled_buffer_2_out = _2 ? shoot : 20'bz;  // Controlled_Buffer controlled_buffer_2
  Pull_Resistor pull_resistor_2 (.node(controlled_buffer_2_out));
  Pull_Resistor pull_resistor_3 (.node(pull_resistor_3_node));
  assign pull_resistor_3_node = _3 ? shoot : 20'bz;  // Controlled_Buffer controlled_buffer_3
  Pull_Resistor pull_resistor_4 (.node(pull_resistor_4_node));
  assign pull_resistor_4_node = _4 ? shoot : 20'bz;  // Controlled_Buffer controlled_buffer_4
  assign or_1_out = controlled_buffer_1_out | out_4;  // OR_Gate or_1, 20 bits wide
  Shifter #(.width(20), .shift("lr")) shifter_1 (.in(or_1_out), .\dist (5'b00001), .out(shifter_1_out));
  assign or_2_out = controlled_buffer_2_out | out_6;  // OR_Gate or_2, 20 bits wide
  Shifter #(.width(20), .shift("lr")) shifter_2 (.in(or_2_out), .\dist (5'b00001), .out(shifter_2_out));
  assign or_3_out = pull_resistor_3_node | out_8;  // OR_Gate or_3, 20 bits wide
  Shifter #(.width(20), .shift("lr")) shifter_3 (.in(or_3_out), .\dist (5'b00001), .out(shifter_3_out));
  assign or_4_out = pull_resistor_4_node | out_10;  // OR_Gate or_4, 20 bits wide
  Shifter #(.width(20), .shift("lr")) shifter_4 (.in(or_4_out), .\dist (5'b00001), .out(shifter_4_out));
  Register #(.width(20)) register_3 (.D(shifter_1_out), .Q(out_4), .clk(in_1));  // open: en, clr
  Register #(.width(20)) register_4 (.D(shifter_2_out), .Q(out_6), .clk(in_1));  // open: en, clr
  Register #(.width(20)) register_5 (.D(shifter_3_out), .Q(out_8), .clk(in_1));  // open: en, clr
  Register #(.width(20)) register_6 (.D(shifter_4_out), .Q(out_10), .clk(in_1));  // open: en, clr
  Pull_Resistor pull_resistor_5 (.node(pull_resistor_5_node));
  assign pull_resistor_5_node = _5 ? shoot : 20'bz;  // Controlled_Buffer controlled_buffer_5
  assign controlled_buffer_6_out = _6 ? shoot : 20'bz;  // Controlled_Buffer controlled_buffer_6
  Pull_Resistor pull_resistor_6 (.node(controlled_buffer_6_out));
  Pull_Resistor pull_resistor_7 (.node(pull_resistor_7_node));
  assign pull_resistor_7_node = _7 ? shoot : 20'bz;  // Controlled_Buffer controlled_buffer_7
  Pull_Resistor pull_resistor_8 (.node(pull_resistor_8_node));
  assign pull_resistor_8_node = _8 ? shoot : 20'bz;  // Controlled_Buffer controlled_buffer_8
  assign or_5_out = pull_resistor_5_node | out_5;  // OR_Gate or_5, 20 bits wide
  assign or_6_out = controlled_buffer_6_out | out_7;  // OR_Gate or_6, 20 bits wide
  assign or_7_out = pull_resistor_7_node | out_9;  // OR_Gate or_7, 20 bits wide
  assign or_8_out = pull_resistor_8_node | out_11;  // OR_Gate or_8, 20 bits wide
  Register #(.width(20)) register_7 (.D(shifter_5_out), .Q(out_5), .clk(in_1));  // open: en, clr
  Shifter #(.width(20), .shift("lr")) shifter_5 (.in(or_5_out), .\dist (5'b00001), .out(shifter_5_out));
  Register #(.width(20)) register_8 (.D(shifter_6_out), .Q(out_7), .clk(in_1));  // open: en, clr
  Shifter #(.width(20), .shift("lr")) shifter_6 (.in(or_6_out), .\dist (5'b00001), .out(shifter_6_out));
  Register #(.width(20)) register_9 (.D(shifter_7_out), .Q(out_9), .clk(in_1));  // open: en, clr
  Shifter #(.width(20), .shift("lr")) shifter_7 (.in(or_7_out), .\dist (5'b00001), .out(shifter_7_out));
  Register #(.width(20)) register_10 (.D(shifter_8_out), .Q(out_11), .clk(in_1));  // open: en, clr
  Shifter #(.width(20), .shift("lr")) shifter_8 (.in(or_8_out), .\dist (5'b00001), .out(shifter_8_out));

  // Other names for the same wires on the sheet: A1[19:0] = out_4; A2[19:0] = out_6; A3[19:0] = out_8;
  //   A4[19:0] = out_10; A5[19:0] = out_5; A6[19:0] = out_7; A7[19:0] = out_9; A8[19:0] = out_11; Tic = in_1
endmodule

module fromCdM8 (
  input  [19:0] in_1,
  input  [19:0] in_2,
  input  [19:0] in_3,
  input  [19:0] in_4,
  input  [19:0] in_5,
  input  [19:0] in_6,
  input  [19:0] in_7,
  input  [19:0] in_8,
  input  [19:0] in_9,
  input  [19:0] in_10,
  input  [7:0] in_11,
  input  [2:0] in_12,
  output [19:0] out_13,
  output [19:0] out_14,
  output [19:0] out_15,
  output [19:0] out_16,
  output [19:0] out_17,
  output [19:0] out_18,
  output [19:0] out_19,
  output [19:0] out_20,
  output [19:0] out_21,
  output [19:0] out_22
);
endmodule

module \or  (
  input  [19:0] in_1,
  input  [19:0] in_2,
  output [19:0] out_3
);

  assign out_3 = in_1 | in_2;  // OR_Gate or_1, 20 bits wide
endmodule

module die (
  input  [19:0] in_1,
  input  [19:0] in_2,
  input  [19:0] in_3,
  input  [19:0] in_4,
  input  [19:0] in_5,
  input  [19:0] in_6,
  input  [19:0] in_7,
  input  [19:0] in_8,
  input  [19:0] in_9,
  input  [19:0] in_10,
  input  [19:0] in_11,
  input  [19:0] in_12,
  input  [19:0] in_13,
  input  [19:0] in_14,
  input  [19:0] in_15,
  input  [19:0] in_16,
  output out_17
);

  wire [19:0] and_1_out, and_2_out, and_3_out, and_4_out, and_5_out, and_6_out, and_7_out, and_8_out,
       or_1_out;

  assign and_1_out = in_1 & in_9;  // AND_Gate and_1, 20 bits wide
  assign and_2_out = in_2 & in_10;  // AND_Gate and_2, 20 bits wide
  assign and_3_out = in_3 & in_11;  // AND_Gate and_3, 20 bits wide
  assign and_4_out = in_4 & in_12;  // AND_Gate and_4, 20 bits wide
  assign and_5_out = in_5 & in_13;  // AND_Gate and_5, 20 bits wide
  assign and_6_out = in_6 & in_14;  // AND_Gate and_6, 20 bits wide
  assign and_7_out = in_7 & in_15;  // AND_Gate and_7, 20 bits wide
  assign and_8_out = in_8 & in_16;  // AND_Gate and_8, 20 bits wide
  assign or_1_out = and_1_out | and_2_out | and_3_out | and_4_out | and_5_out | and_6_out | and_7_out | and_8_out;  // OR_Gate or_1, 20 bits wide
  Comparator #(.width(20)) comparator_1 (.a(or_1_out), .b({20{1'b0}}), .gt(out_17));  // open: eq, lt
endmodule
