// Logisim project car.circ as structural Verilog: 4 circuits, main circuit main
module main (
);

  wire _0xF0_out, _0xF1_out, _0xF2_out, _0xF3_out, _0xF4_out, _0xF5_out, and_1_out, and_2_out, button_2_out,
       button_4_out, button_5_out, button_6_out, car_oper_1_on_off, cdm_8_mark5_1_p1, cdm_8_mark5_1_p2,
       cdm_8_mark5_1_p3, cdm_8_mark5_1_p4, cdm_8_mark5_1_p5, cdm_8_mark5_1_p7, cdm_8_mark5_1_p8, Cl, code,
       comparator_1_gt, decoder_1_out1, demultiplexer_1_out0, demultiplexer_1_out1, demultiplexer_1_out2,
       demultiplexer_1_out3, demultiplexer_1_out4, demultiplexer_1_out5, e, keyboard_1_avail, left, mem,
       not_1_out, not_2_out, not_3_out, not_4_out, or_5_out, pull_resistor_1_node, Rd, register_1_q, Reset,
       right, space;
  wire [2:0] clock_1_out;
  wire [3:0] button_3_out;
  wire [4:4] pull_resistor_3_node;
  wire [6:0] keyboard_1_data;
  wire [7:0] cdm_8_mark5_1_p11, cdm_8_mark5_1_p12, cdm_8_mark5_1_p13, controlled_buffer_3_out,
       controlled_buffer_4_out, controlled_buffer_5_out, controlled_buffer_6_out, controlled_buffer_7_out,
       Input_0xF3, Input_0xF4, Input_0xF5, Output_0xF0, Output_0xF1, Output_0xF2, ram_1_data, rom_1_data,
       rom_2_data, rom_3_data, rom_4_data;
  wire [15:0] car_oper_1_out_15;
  wire [19:0] car_oper_1_disp0, car_oper_1_disp1, car_oper_1_disp2, car_oper_1_disp3, car_oper_1_disp4,
       car_oper_1_disp5, car_oper_1_disp6, car_oper_1_disp7, car_oper_1_disp8, car_oper_1_disp9;

  Button button_1 (.out(button_3_out[3]));
  or or_1 (button_3_out[2], left, button_2_out);
  Button button_2 (.out(button_2_out));
  DotMatrix #(.matrixcols(10), .matrixrows(20)) dotmatrix_1 (
    .col0(car_oper_1_disp0), .col1(car_oper_1_disp1), .col2(car_oper_1_disp2), .col3(car_oper_1_disp3),
    .col4(car_oper_1_disp4), .col5(car_oper_1_disp5), .col6(car_oper_1_disp6), .col7(car_oper_1_disp7),
    .col8(car_oper_1_disp8), .col9(car_oper_1_disp9));
  car_oper car_oper_1 (
    .key(button_3_out), .Disp0(car_oper_1_disp0), .Disp1(car_oper_1_disp1), .Disp2(car_oper_1_disp2),
    .Disp3(car_oper_1_disp3), .Disp4(car_oper_1_disp4), .Disp5(car_oper_1_disp5), .Disp6(car_oper_1_disp6),
    .Disp7(car_oper_1_disp7), .Disp8(car_oper_1_disp8), .Disp9(car_oper_1_disp9), .out_15(car_oper_1_out_15),
    .ON_OFF(car_oper_1_on_off), .in_4(clock_1_out), .in_3(1'b1), .in_1(Output_0xF0), .out_16(Input_0xF3),
    .out_17(Reset));
  Button button_3 (.out(button_3_out[0]));
  or or_2 (button_3_out[1], button_4_out, right);
  Button button_4 (.out(button_4_out));
  // Probe on cdm_8_mark5_1_p1
  not not_1 (not_1_out, register_1_q);
  or or_3 (clock_1_out[2], space, button_5_out);
  Button button_5 (.out(button_5_out));
  // Probe on cdm_8_mark5_1_p4
  // Probe on cdm_8_mark5_1_p5
  // Probe on cdm_8_mark5_1_p3
  // Probe on cdm_8_mark5_1_p2
  not not_2 (not_2_out, register_1_q);
  Register #(.width(1)) register_1 (.D(not_2_out), .Q(register_1_q), .clk(Reset), .clr(Output_0xF0[6]));  // open: en
  // Probe on nothing
  // Probe on car_oper_1_out_15
  Clock clock_1 (.out(clock_1_out[0]));
  or or_4 (clock_1_out[1], button_6_out, e);
  Button button_6 (.out(button_6_out));
  // Probe on cdm_8_mark5_1_p7
  Pull_Resistor pull_resistor_1 (.node(pull_resistor_1_node));
  assign pull_resistor_1_node = register_1_q ? Cl : 1'bz;  // Controlled_Buffer controlled_buffer_1
  Clock clock_2 (.out(Cl));
  // Probe on nothing
  Decoder #(.disabled(0)) decoder_1 (.out0(code), .out1(decoder_1_out1), .sel(cdm_8_mark5_1_p8), .en(mem));
  // CdM_8_mark5 cdm_8_mark5_1: pin names not known; wires that end beside it: cdm_8_mark5_1_p1, cdm_8_mark5_1_p2, cdm_8_mark5_1_p3, cdm_8_mark5_1_p4, cdm_8_mark5_1_p5, pull_resistor_1_node, cdm_8_mark5_1_p7, cdm_8_mark5_1_p8, mem, Rd, cdm_8_mark5_1_p11, cdm_8_mark5_1_p12, cdm_8_mark5_1_p13
  not not_3 (not_3_out, Rd);
  assign cdm_8_mark5_1_p13 = Rd ? controlled_buffer_7_out : 8'bz;  // Controlled_Buffer controlled_buffer_2
  Keyboard #(.buflen(20)) keyboard_1 (
    .clk(keyboard_1_avail), .avail(keyboard_1_avail), .data(keyboard_1_data));  // open: re, clr
  assign controlled_buffer_3_out = 1'b1 ? cdm_8_mark5_1_p11 : 8'bz;  // Controlled_Buffer controlled_buffer_3
  assign controlled_buffer_4_out = 1'b0 ? cdm_8_mark5_1_p11 : 8'bz;  // Controlled_Buffer controlled_buffer_4
  assign controlled_buffer_5_out = 1'b0 ? cdm_8_mark5_1_p11 : 8'bz;  // Controlled_Buffer controlled_buffer_5
  assign controlled_buffer_6_out = 1'b0 ? cdm_8_mark5_1_p11 : 8'bz;  // Controlled_Buffer controlled_buffer_6
  Pull_Resistor pull_resistor_2 (.node(cdm_8_mark5_1_p11));
  assign controlled_buffer_7_out = not_3_out ? cdm_8_mark5_1_p12 : 8'bz;  // Controlled_Buffer controlled_buffer_7
  Comparator #(.mode("unsigned")) comparator_1 (
    .a(cdm_8_mark5_1_p11), .b(8'hef), .gt(comparator_1_gt));  // open: eq, lt
  and and_1 (and_1_out, decoder_1_out1, or_5_out);
  // Probe on keyboard_1_data
  // Probe on keyboard_1_data
  ROM rom_1 (.addr(controlled_buffer_3_out), .data(rom_1_data), .sel(code));
  ROM rom_2 (.addr(controlled_buffer_4_out), .data(rom_2_data), .sel(code));
  ROM rom_3 (.addr(controlled_buffer_5_out), .data(rom_3_data), .sel(code));
  ROM rom_4 (.addr(controlled_buffer_6_out), .data(rom_4_data), .sel(code));
  RAM #(.bus("separate")) ram_1 (
    .addr(cdm_8_mark5_1_p11), .din(controlled_buffer_7_out), .data(ram_1_data), .sel(and_1_out),
    .clk(pull_resistor_1_node), .ld(Rd), .clr(not_1_out));  // open: str
  Comparator #(.width(7)) comparator_2 (.a(keyboard_1_data), .b(7'b0100000), .eq(space));  // open: gt, lt
  Comparator #(.width(7)) comparator_3 (.a(keyboard_1_data), .b(7'b1100001), .eq(left));  // open: gt, lt
  Comparator #(.width(7)) comparator_4 (.a(keyboard_1_data), .b(7'b1100100), .eq(right));  // open: gt, lt
  Comparator #(.width(7)) comparator_5 (.a(keyboard_1_data), .b(7'b1100101), .eq(e));  // open: gt, lt
  and and_2 (and_2_out, pull_resistor_1_node, decoder_1_out1, comparator_1_gt);
  Pull_Resistor pull_resistor_3 (.node({pull_resistor_3_node[4], cdm_8_mark5_1_p11[3:0]}));
  assign ram_1_data = 1'b1 ? rom_1_data : 8'bz;  // Controlled_Buffer controlled_buffer_8
  assign ram_1_data = 1'b0 ? rom_2_data : 8'bz;  // Controlled_Buffer controlled_buffer_9
  assign ram_1_data = 1'b0 ? rom_3_data : 8'bz;  // Controlled_Buffer controlled_buffer_10
  assign ram_1_data = 1'b0 ? rom_4_data : 8'bz;  // Controlled_Buffer controlled_buffer_11
  Demultiplexer #(.select(5), .disabled(0)) demultiplexer_1 (
    .out0(demultiplexer_1_out0), .out1(demultiplexer_1_out1), .out2(demultiplexer_1_out2),
    .out3(demultiplexer_1_out3), .out4(demultiplexer_1_out4), .out5(demultiplexer_1_out5), .in(1'b1),
    .sel({pull_resistor_3_node[4], cdm_8_mark5_1_p11[3:0]}), .en(and_2_out));  // open: out6, out7, out8, out9, out10, out11, out12, out13, out14, out15, out16, out17, out18, out19, out20, out21, out22, out23, out24, out25, out26, out27, out28, out29, out30, out31
  assign controlled_buffer_7_out = not_4_out ? ram_1_data : 8'bz;  // Controlled_Buffer controlled_buffer_12
  not not_4 (not_4_out, or_5_out);
  and _0xF0 (_0xF0_out, demultiplexer_1_out0, ~Rd);  // AND_Gate
  and _0xF1 (_0xF1_out, demultiplexer_1_out1, ~Rd);  // AND_Gate
  and _0xF2 (_0xF2_out, demultiplexer_1_out2, ~Rd);  // AND_Gate
  assign controlled_buffer_7_out = _0xF3_out ? Input_0xF3 : 8'bz;  // Controlled_Buffer controlled_buffer_13
  and _0xF3 (_0xF3_out, demultiplexer_1_out3, Rd);
  assign controlled_buffer_7_out = _0xF4_out ? Input_0xF4 : 8'bz;  // Controlled_Buffer controlled_buffer_14
  and _0xF4 (_0xF4_out, demultiplexer_1_out4, Rd);
  assign controlled_buffer_7_out = _0xF5_out ? Input_0xF5 : 8'bz;  // Controlled_Buffer controlled_buffer_15
  and _0xF5 (_0xF5_out, demultiplexer_1_out5, Rd);
  Register register_2 (.D(controlled_buffer_7_out), .Q(Output_0xF0), .clk(_0xF0_out), .clr(not_1_out));  // open: en
  Register register_3 (.D(controlled_buffer_7_out), .Q(Output_0xF1), .clk(_0xF1_out), .clr(not_1_out));  // open: en
  Register register_4 (.D(controlled_buffer_7_out), .Q(Output_0xF2), .clk(_0xF2_out), .clr(not_1_out));  // open: en
  or or_5 (or_5_out, _0xF5_out, _0xF4_out, _0xF3_out, _0xF2_out, _0xF1_out, _0xF0_out, comparator_1_gt);
  // CdM_8 cdm_8_1: pin names not known

  // Notes on the sheet:
  //   contents of rom_1 (hex, n*v repeats v):
  //   d0 f3 b0 d1 4 d2 2 d3 1 41 e1 1e 42 e1 17 d1 f0 d3 40 5c a4 ee 1c d0 f0 d1 c0 a1 ee 2e 43 e1 29 d1
  //   f0 d3 40 5c a4 ee 2e d0 f0 d1 c0 a1 ee 0 d4
  //   contents of rom_2 (hex, n*v repeats v):
  //   d0 f3 b0 8c d1 f0 a4 d4
  //   contents of rom_3 (hex, n*v repeats v):
  //   d0 10 d0 36 d1 0 31 7 d1 f3 a7 d4
  //   contents of rom_4 (hex, n*v repeats v):
  //   d0 10 d0 e8 d1 0 31 7 d1 f3 a7 d4
  //   Cars
endmodule

module car_oper (
  input  [7:0] in_1,
  input  [3:0] key,
  input  in_3,
  input  [2:0] in_4,
  output [19:0] Disp0,
  output [19:0] Disp1,
  output [19:0] Disp2,
  output [19:0] Disp4,
  output [19:0] Disp3,
  output [19:0] Disp5,
  output [19:0] Disp7,
  output [19:0] Disp6,
  output [19:0] Disp8,
  output [19:0] Disp9,
  output [15:0] out_15,
  output [7:0] out_16,
  output out_17,
  output ON_OFF
);

  wire and_1_out, and_2_out, and_3_out, and_4_out, and_5_out, bitfinder_1_found, car, comparator_1_eq,
       counter_2_carry, multiplexer_1_out, multiplexer_3_out, not_1_out, not_2_out, not_4_out, or_6_out,
       pull_resistor_2_node, random_1_out, register_3_q, Takt;
  wire [3:0] controlled_buffer_3_out, m1, m2, m4, m5, register_7_q, register_8_q, register_9_q,
       register_10_q, shifter_1_out, shifter_2_out, shifter_3_out, shifter_4_out;
  wire [7:0] counter_1_q, multiplexer_5_out, pull_resistor_3_node;
  wire [19:0] krai_1_out_2, krai_2_out_2, Left, multiplexer_2_out, multiplexer_4_out, multiplexer_6_out,
       multiplexer_7_out, next_1_out_3, next_2_out_3, or_1_out, or_2_out, or_5_out, or_7_out, register_1_q,
       register_6_q, Right;

  assign Disp0 = in_3 ? krai_1_out_2 : 20'bz;  // Controlled_Buffer controlled_buffer_1
  krai krai_1 (.in_1(next_1_out_3), .out_2(krai_1_out_2));
  next next_1 (.in_1(krai_1_out_2), .in_2(Takt), .out_3(next_1_out_3));
  assign Disp1 = in_3 ? {20{1'b0}} : 20'bz;  // Controlled_Buffer controlled_buffer_2
  assign controlled_buffer_3_out = not_1_out ? key : 4'bz;  // Controlled_Buffer controlled_buffer_3
  Pull_Resistor pull_resistor_1 (.node(controlled_buffer_3_out));
  not not_1 (not_1_out, ON_OFF);
  assign Disp2 = in_3 ? or_1_out : 20'bz;  // Controlled_Buffer controlled_buffer_4
  assign or_1_out = register_1_q | multiplexer_2_out;  // OR_Gate or_1, 20 bits wide
  Multiplexer #(.enable("false")) multiplexer_1 (
    .in0(car), .in1(1'b0), .out(multiplexer_1_out), .sel(controlled_buffer_3_out[2]));
  BitFinder #(.width(4)) bitfinder_1 (.in(controlled_buffer_3_out), .found(bitfinder_1_found));  // open: index
  Multiplexer #(.width(20), .enable("false")) multiplexer_2 (
    .in0(20'h5), .in1({20{1'b0}}), .out(multiplexer_2_out), .sel(car));
  Register #(.width(20)) register_1 (
    .D({m1[0], register_1_q[19:1]}), .Q(register_1_q), .clk(Takt), .clr(in_1[7]));  // open: en
  Register #(.width(1), .trigger("falling")) register_2 (
    .D(multiplexer_3_out), .Q(car), .clk(bitfinder_1_found));  // open: en, clr
  Multiplexer #(.enable("false")) multiplexer_3 (
    .in0(multiplexer_1_out), .in1(1'b1), .out(multiplexer_3_out), .sel(controlled_buffer_3_out[1]));
  Pull_Resistor pull_resistor_2 (.node(pull_resistor_2_node));
  and and_1 (and_1_out, ~ON_OFF, in_3);  // AND_Gate
  assign Disp3 = in_3 ? or_2_out : 20'bz;  // Controlled_Buffer controlled_buffer_5
  assign or_2_out = Left | multiplexer_4_out;  // OR_Gate or_2, 20 bits wide
  assign out_16 = in_3 ? {pull_resistor_3_node[7:3], car, pull_resistor_3_node[1:0]} : 8'bz;  // Controlled_Buffer controlled_buffer_6
  Pull_Resistor pull_resistor_3 (.node({pull_resistor_3_node[7:3], car, pull_resistor_3_node[1:0]}));
  Counter counter_1 (
    .Q(counter_1_q), .clk(pull_resistor_2_node), .clr(comparator_1_eq));  // open: load, D, count, carry
  assign pull_resistor_2_node = and_1_out ? in_4[0] : 1'bz;  // Controlled_Buffer controlled_buffer_7
  not not_2 (not_2_out, register_3_q);
  Register #(.width(1)) register_3 (.D(not_2_out), .Q(register_3_q), .clk(in_4[2]));  // open: en, clr
  Multiplexer #(.width(20), .enable("false")) multiplexer_4 (
    .in0(20'he), .in1({20{1'b0}}), .out(multiplexer_4_out), .sel(car));
  Register #(.width(20)) register_4 (.D({m2[0], Left[19:1]}), .Q(Left), .clk(Takt), .clr(in_1[7]));  // open: en
  or or_3 (pull_resistor_3_node[0], Right[3], Right[2], Right[1]);
  or or_4 (pull_resistor_3_node[1], Left[3], Left[2], Left[1]);
  not not_3 (pull_resistor_3_node[6], Takt);
  Comparator #(.mode("unsigned")) comparator_1 (
    .a(counter_1_q), .b(multiplexer_5_out), .eq(comparator_1_eq));  // open: gt, lt
  Multiplexer #(.width(8), .enable("false")) multiplexer_5 (
    .in0(8'h80), .in1(8'h10), .out(multiplexer_5_out), .sel(register_3_q));
  assign Disp5 = in_3 ? or_5_out : 20'bz;  // Controlled_Buffer controlled_buffer_8
  assign or_5_out = register_6_q | multiplexer_6_out;  // OR_Gate or_5, 20 bits wide
  Multiplexer #(.width(20), .enable("false")) multiplexer_6 (
    .in0({20{1'b0}}), .in1(20'h5), .out(multiplexer_6_out), .sel(car));
  Counter #(.width(4), .max('ha)) counter_2 (.carry(counter_2_carry), .clk(Takt));  // open: load, D, count, Q, clr
  assign out_17 = in_3 ? Takt : 1'bz;  // Controlled_Buffer controlled_buffer_9
  Register #(.width(1)) register_5 (.D(pull_resistor_3_node[6]), .Q(Takt), .clk(comparator_1_eq));  // open: en, clr
  and and_2 (and_2_out, in_4[2], ON_OFF);
  and and_3 (and_3_out, ~ON_OFF, in_4[1]);  // AND_Gate
  Register #(.width(20)) register_6 (
    .D({m4[0], register_6_q[19:1]}), .Q(register_6_q), .clk(Takt), .clr(in_1[7]));  // open: en
  Register #(.width(4)) register_7 (.D(shifter_1_out), .Q(register_7_q), .clk(Takt), .clr(in_1[7]));  // open: en
  Shifter #(.width(4), .shift("lr")) shifter_1 (.in(m1), .\dist (2'b01), .out(shifter_1_out));
  Register #(.width(4)) register_8 (.D(shifter_2_out), .Q(register_8_q), .clk(Takt), .clr(in_1[7]));  // open: en
  Shifter #(.width(4), .shift("lr")) shifter_2 (.in(m2), .\dist (2'b01), .out(shifter_2_out));
  Shifter #(.width(4), .shift("lr")) shifter_3 (.in(m4), .\dist (2'b01), .out(shifter_3_out));
  Register #(.width(4)) register_9 (.D(shifter_3_out), .Q(register_9_q), .clk(Takt), .clr(in_1[7]));  // open: en
  Shifter #(.width(4), .shift("lr")) shifter_4 (.in(m5), .\dist (2'b01), .out(shifter_4_out));
  Register #(.width(4)) register_10 (.D(shifter_4_out), .Q(register_10_q), .clk(Takt), .clr(in_1[7]));  // open: en
  Random #(.width(1)) random_1 (.clk(counter_2_carry), .out(random_1_out));  // open: next, clr
  not not_4 (not_4_out, ON_OFF);
  Register #(.width(1), .trigger("falling")) register_11 (.D(not_4_out), .Q(ON_OFF), .clk(or_6_out));  // open: en, clr
  or or_6 (or_6_out, and_2_out, in_1[7], and_3_out);
  assign Disp6 = in_3 ? or_7_out : 20'bz;  // Controlled_Buffer controlled_buffer_10
  assign or_7_out = Right | multiplexer_7_out;  // OR_Gate or_7, 20 bits wide
  Multiplexer #(.width(20), .enable("false")) multiplexer_7 (
    .in0({20{1'b0}}), .in1(20'he), .out(multiplexer_7_out), .sel(car));
  Multiplexer #(.width(4), .disabled(0), .enable("false")) multiplexer_8 (
    .in0(register_7_q), .in1(4'b0101), .out(m1), .sel(and_4_out));
  Multiplexer #(.width(4), .disabled(0), .enable("false")) multiplexer_9 (
    .in0(register_8_q), .in1(4'b1110), .out(m2), .sel(and_4_out));
  and and_4 (and_4_out, random_1_out, counter_2_carry);
  Multiplexer #(.width(4), .disabled(0), .enable("false")) multiplexer_10 (
    .in0(register_9_q), .in1(4'b0101), .out(m4), .sel(and_5_out));
  Multiplexer #(.width(4), .disabled(0), .enable("false")) multiplexer_11 (
    .in0(register_10_q), .in1(4'b1110), .out(m5), .sel(and_5_out));
  and and_5 (and_5_out, ~random_1_out, counter_2_carry);  // AND_Gate
  assign Disp8 = in_3 ? {20{1'b0}} : 20'bz;  // Controlled_Buffer controlled_buffer_11
  Register #(.width(20)) register_12 (.D({m5[0], Right[19:1]}), .Q(Right), .clk(Takt), .clr(in_1[7]));  // open: en
  Counter #(.width(16), .max('hffff)) counter_3 (
    .Q(out_15), .clk(counter_2_carry), .clr(in_1[7]));  // open: load, D, count, carry
  assign Disp9 = in_3 ? krai_2_out_2 : 20'bz;  // Controlled_Buffer controlled_buffer_12
  krai krai_2 (.in_1(next_2_out_3), .out_2(krai_2_out_2));
  next next_2 (.in_1(krai_2_out_2), .in_2(Takt), .out_3(next_2_out_3));

  assign Disp4 = Disp2;
  assign Disp7 = Disp5;

  // Other names for the same wires on the sheet: boom = in_1[7]; sel = in_3; stop = ON_OFF
endmodule

module next (
  input  [19:0] in_1,
  input  in_2,
  output [19:0] out_3
);

  wire [19:0] shifter_1_out;

  Shifter #(.width(20), .shift("lr")) shifter_1 (.in(in_1), .\dist (5'b00001), .out(shifter_1_out));
  Register #(.width(20)) register_1 (.D(shifter_1_out), .Q(out_3), .clk(in_2));  // open: en, clr
endmodule

module krai (
  input  [19:0] in_1,
  output [19:0] out_2
);

  wire [19:19] or_1_out;

  assign {or_1_out[19], out_2[18:0]} = in_1 | 20'h80000;  // OR_Gate or_1, 20 bits wide
  and and_1 (out_2[19], or_1_out[19], ~out_2[16]);  // AND_Gate
endmodule
