// Logisim project snake_Test.circ as structural Verilog: 4 circuits, main circuit main
module main (
);

  wire _0xF0_out, _0xF1_out, _0xF2_out, _0xF3_out, _0xF4_out, _0xF5_out, and_1_out, and_2_out, button_1_out,
       button_2_out, button_3_out, button_4_out, button_5_out, button_6_out, button_7_out, cdm_8_mark5_1_p2,
       cdm_8_mark5_1_p4, cdm_8_mark5_1_p5, cdm_8_mark5_1_p6, cdm_8_mark5_1_p7, cdm_8_mark5_1_p8, Cl, code,
       comparator_1_gt, cpu_snake_1_d___1, decoder_1_out1, demultiplexer_1_out0, demultiplexer_1_out1,
       demultiplexer_1_out2, demultiplexer_1_out3, demultiplexer_1_out4, demultiplexer_1_out5, down, e,
       keyboard_1_avail, left, mem, not_1_out, not_2_out, not_3_out, not_4_out, or_7_out,
       pull_resistor_1_node, Rd, register_1_q, Reset, right, space, up;
  wire [2:1] or_5_out;
  wire [3:0] or_3_out;
  wire [4:4] pull_resistor_3_node;
  wire [6:0] keyboard_1_data;
  wire [7:0] cdm_8_mark5_1_p11, cdm_8_mark5_1_p12, cdm_8_mark5_1_p13, controlled_buffer_3_out,
       controlled_buffer_4_out, controlled_buffer_5_out, controlled_buffer_6_out, controlled_buffer_7_out,
       Input_0xF3, Input_0xF4, Input_0xF5, Output_0xF0, Output_0xF1, Output_0xF2, ram_1_data, rom_1_data,
       rom_2_data, rom_3_data, rom_4_data;
  wire [15:0] cpu_snake_1_out_16;
  wire [19:0] cpu_snake_1_disp0, cpu_snake_1_disp1, cpu_snake_1_disp2, cpu_snake_1_disp3, cpu_snake_1_disp4,
       cpu_snake_1_disp5, cpu_snake_1_disp6, cpu_snake_1_disp7, cpu_snake_1_disp8, cpu_snake_1_disp9;

  or or_1 (or_3_out[3], down, button_2_out);
  or or_2 (or_3_out[2], left, button_1_out);
  Button button_1 (.out(button_1_out));
  Button button_2 (.out(button_2_out));
  not not_1 (not_1_out, register_1_q);
  or or_3 (or_3_out[0], button_3_out, up);
  or or_4 (or_3_out[1], button_4_out, right);
  Button button_3 (.out(button_3_out));
  Button button_4 (.out(button_4_out));
  not not_2 (not_2_out, register_1_q);
  Register #(.width(1)) register_1 (.D(not_2_out), .Q(register_1_q), .clk(Reset), .clr(Output_0xF0[6]));  // open: en
  Button button_5 (.out(button_5_out));
  // Probe on cdm_8_mark5_1_p5
  // Probe on cdm_8_mark5_1_p4
  // Probe on cdm_8_mark5_1_p2
  // Probe on cdm_8_mark5_1_p6
  // Probe on nothing
  Pull_Resistor pull_resistor_1 (.node(pull_resistor_1_node));
  assign pull_resistor_1_node = register_1_q ? Cl : 1'bz;  // Controlled_Buffer controlled_buffer_1
  DotMatrix #(.matrixcols(10), .matrixrows(20)) dotmatrix_1 (
    .col0(cpu_snake_1_disp0), .col1(cpu_snake_1_disp1), .col2(cpu_snake_1_disp2), .col3(cpu_snake_1_disp3),
    .col4(cpu_snake_1_disp4), .col5(cpu_snake_1_disp5), .col6(cpu_snake_1_disp6), .col7(cpu_snake_1_disp7),
    .col8(cpu_snake_1_disp8), .col9(cpu_snake_1_disp9));
  CPU_snake cpu_snake_1 (
    .S___3(or_3_out), .W___0(1'b1), .out_16(cpu_snake_1_out_16), .Disp0(cpu_snake_1_disp0),
    .Disp1(cpu_snake_1_disp1), .Disp2(cpu_snake_1_disp2), .Disp3(cpu_snake_1_disp3),
    .Disp4(cpu_snake_1_disp4), .Disp5(cpu_snake_1_disp5), .Disp6(cpu_snake_1_disp6),
    .Disp7(cpu_snake_1_disp7), .Disp8(cpu_snake_1_disp8), .Disp9(cpu_snake_1_disp9),
    .D___1(cpu_snake_1_d___1), .in_3({or_5_out, Cl}), .X___old_Kyda(Input_0xF3), .Y___new_Kyda_2(Input_0xF4),
    .X(Output_0xF0), .Y___new_Kyda(Output_0xF1), .out_20(Reset));
  Decoder #(.disabled(0)) decoder_1 (.out0(code), .out1(decoder_1_out1), .sel(cdm_8_mark5_1_p8), .en(mem));
  // Probe on cdm_8_mark5_1_p7
  // CdM_8_mark5 cdm_8_mark5_1: pin names not known; wires that end beside it: button_5_out, cdm_8_mark5_1_p2, pull_resistor_1_node, cdm_8_mark5_1_p4, cdm_8_mark5_1_p5, cdm_8_mark5_1_p6, cdm_8_mark5_1_p7, cdm_8_mark5_1_p8, mem, Rd, cdm_8_mark5_1_p11, cdm_8_mark5_1_p12, cdm_8_mark5_1_p13
  not not_3 (not_3_out, Rd);
  assign cdm_8_mark5_1_p13 = Rd ? controlled_buffer_7_out : 8'bz;  // Controlled_Buffer controlled_buffer_2
  assign controlled_buffer_3_out = 1'b1 ? cdm_8_mark5_1_p11 : 8'bz;  // Controlled_Buffer controlled_buffer_3
  assign controlled_buffer_4_out = 1'b0 ? cdm_8_mark5_1_p11 : 8'bz;  // Controlled_Buffer controlled_buffer_4
  assign controlled_buffer_5_out = 1'b0 ? cdm_8_mark5_1_p11 : 8'bz;  // Controlled_Buffer controlled_buffer_5
  assign controlled_buffer_6_out = 1'b0 ? cdm_8_mark5_1_p11 : 8'bz;  // Controlled_Buffer controlled_buffer_6
  Pull_Resistor pull_resistor_2 (.node(cdm_8_mark5_1_p11));
  assign controlled_buffer_7_out = not_3_out ? cdm_8_mark5_1_p12 : 8'bz;  // Controlled_Buffer controlled_buffer_7
  // Probe on cpu_snake_1_out_16
  Clock clock_1 (.out(Cl));
  or or_5 (or_5_out[1], button_6_out, e);
  or or_6 (or_5_out[2], space, button_7_out);
  Button button_6 (.out(button_6_out));
  Button button_7 (.out(button_7_out));
  Comparator #(.mode("unsigned")) comparator_1 (
    .a(cdm_8_mark5_1_p11), .b(8'hef), .gt(comparator_1_gt));  // open: eq, lt
  and and_1 (and_1_out, decoder_1_out1, or_7_out);
  Keyboard #(.buflen(20)) keyboard_1 (
    .clk(keyboard_1_avail), .avail(keyboard_1_avail), .data(keyboard_1_data));  // open: re, clr
  ROM rom_1 (.addr(controlled_buffer_3_out), .data(rom_1_data), .sel(code));
  ROM rom_2 (.addr(controlled_buffer_4_out), .data(rom_2_data), .sel(code));
  ROM rom_3 (.addr(controlled_buffer_5_out), .data(rom_3_data), .sel(code));
  ROM rom_4 (.addr(controlled_buffer_6_out), .data(rom_4_data), .sel(code));
  RAM #(.bus("separate")) ram_1 (
    .addr(cdm_8_mark5_1_p11), .din(controlled_buffer_7_out), .data(ram_1_data), .sel(and_1_out),
    .clk(pull_resistor_1_node), .ld(Rd), .clr(not_1_out));  // open: str
  and and_2 (and_2_out, pull_resistor_1_node, decoder_1_out1, comparator_1_gt);
  Pull_Resistor pull_resistor_3 (.node({pull_resistor_3_node[4], cdm_8_mark5_1_p11[3:0]}));
  assign ram_1_data = 1'b1 ? rom_1_data : 8'bz;  // Controlled_Buffer controlled_buffer_8
  assign ram_1_data = 1'b0 ? rom_2_data : 8'bz;  // Controlled_Buffer controlled_buffer_9
  assign ram_1_data = 1'b0 ? rom_3_data : 8'bz;  // Controlled_Buffer controlled_buffer_10
  assign ram_1_data = 1'b0 ? rom_4_data : 8'bz;  // Controlled_Buffer controlled_buffer_11
  Demultiplexer #(.select(5), .disabled(0)) demultiplexer_1 (
    .out0(demultiplexer_1_out0), .out1(demultiplexer_1_out1), .out2(demultiplexer_1_out2),
    .out3(demultiplexer_1_out3), .out4(demultiplexer_1_out4), .out5(demultiplexer_1_out5), .in(1'b1),
    .sel({pull_resistor_3_node[4], cdm_8_mark5_1_p11[3:0]}), .en(and_2_out));  // open: out6, out7, out8, out9, out10, out11, out12, out13, out14, out15, out16, out17, out18, out19, out20, out21, out22, out23, out24, out25, out26, out27, out28, out29, out30, out31
  assign controlled_buffer_7_out = not_4_out ? ram_1_data : 8'bz;  // Controlled_Buffer controlled_buffer_12
  not not_4 (not_4_out, or_7_out);
  Comparator #(.width(7)) comparator_2 (.a(keyboard_1_data), .b(7'b0100000), .eq(space));  // open: gt, lt
  Comparator #(.width(7)) comparator_3 (.a(keyboard_1_data), .b(7'b1100001), .eq(left));  // open: gt, lt
  Comparator #(.width(7)) comparator_4 (.a(keyboard_1_data), .b(7'b1100100), .eq(right));  // open: gt, lt
  Comparator #(.width(7)) comparator_5 (.a(keyboard_1_data), .b(7'b1100101), .eq(e));  // open: gt, lt
  Comparator #(.width(7)) comparator_6 (.a(keyboard_1_data), .b(7'b1110011), .eq(down));  // open: gt, lt
  Comparator #(.width(7)) comparator_7 (.a(keyboard_1_data), .b(7'b1110111), .eq(up));  // open: gt, lt
  and _0xF0 (_0xF0_out, demultiplexer_1_out0, ~Rd);  // AND_Gate
  and _0xF1 (_0xF1_out, demultiplexer_1_out1, ~Rd);  // AND_Gate
  and _0xF2 (_0xF2_out, demultiplexer_1_out2, ~Rd);  // AND_Gate
  assign controlled_buffer_7_out = _0xF3_out ? Input_0xF3 : 8'bz;  // Controlled_Buffer controlled_buffer_13
  and _0xF3 (_0xF3_out, demultiplexer_1_out3, Rd);
  assign controlled_buffer_7_out = _0xF4_out ? Input_0xF4 : 8'bz;  // Controlled_Buffer controlled_buffer_14
  and _0xF4 (_0xF4_out, demultiplexer_1_out4, Rd);
  assign controlled_buffer_7_out = _0xF5_out ? Input_0xF5 : 8'bz;  // Controlled_Buffer controlled_buffer_15
  and _0xF5 (_0xF5_out, demultiplexer_1_out5, Rd);
  Register register_2 (.D(controlled_buffer_7_out), .Q(Output_0xF0), .clk(_0xF0_out), .clr(not_1_out));  // open: en
  Register register_3 (.D(controlled_buffer_7_out), .Q(Output_0xF1), .clk(_0xF1_out), .clr(not_1_out));  // open: en
  Register register_4 (.D(controlled_buffer_7_out), .Q(Output_0xF2), .clk(_0xF2_out), .clr(not_1_out));  // open: en
  or or_7 (or_7_out, _0xF5_out, _0xF4_out, _0xF3_out, _0xF2_out, _0xF1_out, _0xF0_out, comparator_1_gt);
  Pull_Resistor pull_resistor_4 (.node(Output_0xF0));
  Pull_Resistor pull_resistor_5 (.node(Output_0xF1));
  Pull_Resistor pull_resistor_6 (.node(Output_0xF2));
  Pull_Resistor pull_resistor_7 (.node(Input_0xF3));
  Pull_Resistor pull_resistor_8 (.node(Input_0xF4));
  Pull_Resistor pull_resistor_9 (.node(Input_0xF5));

  // Notes on the sheet:
  //   Head X and old Kyda
  //   Head Y and new Kyda
  //   Head X and old Kyda
  //   Head Y and new Kyda
  //   contents of rom_1 (hex, n*v repeats v):
  //   d0 f3 b0 d1 f4 b5 d2 3 42 d3 3 47 1b d2 3 7e e1 17 d3 3 43 ee 1a d3 3 47 98 98 98 99 99 d2 3 7e e1
  //   27 89 ee 38 d2 2 7e e1 2f 88 ee 38 d2 1 7e e1 37 8c ee 38 8d 0 e5 3f d0 9 ee 46 d2 9 78 e5 46 d0 0 5
  //   e5 4d d1 13 ee 54 d2 13 79 e5 54 d1 0 95 95 1d d3 f1 ad d3 40 5c d2 f0 a8 ee 0 d4
  //   contents of rom_2 (hex, n*v repeats v):
  //   d0 f3 b0 8c d1 f0 a4 d4
  //   contents of rom_3 (hex, n*v repeats v):
  //   d0 10 d0 36 d1 0 31 7 d1 f3 a7 d4
  //   contents of rom_4 (hex, n*v repeats v):
  //   d0 f3 b0 d1 4 d2 2 d3 1 41 e1 1e 42 e1 17 d1 f0 d3 40 5c a4 ee 1c d0 f0 d1 c0 a1 ee 2e 43 e1 29 d1
  //   f0 d3 40 5c a4 ee 2e d0 f0 d1 c0 a1 ee 0 d4
  //   Cars
endmodule

module CPU_snake (
  input  W___0,
  input  [3:0] S___3,
  input  [2:0] in_3,
  input  [7:0] X,
  input  [7:0] Y___new_Kyda,
  output [19:0] Disp0,
  output [19:0] Disp1,
  output [19:0] Disp2,
  output [19:0] Disp3,
  output [19:0] Disp4,
  output [19:0] Disp5,
  output [19:0] Disp6,
  output [19:0] Disp7,
  output [19:0] Disp8,
  output [19:0] Disp9,
  output [15:0] out_16,
  output D___1,
  output [7:0] Y___new_Kyda_2,
  output [7:0] X___old_Kyda,
  output out_20
);

  wire and_1_out, and_2_out, and_3_out, apple, bitfinder_1_found, comparator_1_eq, comparator_2_gt,
       comparator_3_gt, controlled_buffer_1_out, controlled_buffer_12_out, decoder_1_out0, decoder_1_out1,
       decoder_1_out2, decoder_1_out3, decoder_1_out4, decoder_1_out5, decoder_1_out6, decoder_1_out7,
       decoder_1_out8, decoder_1_out9, decoder_2_out0, decoder_2_out1, decoder_2_out2, decoder_2_out3,
       decoder_2_out4, decoder_2_out5, decoder_2_out6, decoder_2_out7, decoder_2_out8, decoder_2_out9,
       element_1_apple, element_1_boom_2, element_2_apple, element_2_boom_2, element_3_apple,
       element_3_boom_2, element_4_apple, element_4_boom_2, element_5_apple, element_5_boom_2,
       element_6_apple, element_6_boom_2, element_7_apple, element_7_boom_2, element_8_apple,
       element_8_boom_2, element_9_apple, element_9_boom_2, element_10_apple, element_10_boom_2, not_1_out,
       not_2_out, not_3_out, not_4_out, or_1_out, or_2_out, or_3_out, Takt, Tik;
  wire [1:0] bitfinder_1_index, Kyda, Old_Kyda;
  wire [3:0] multiplexer_1_out, random_1_out, snake_X, subtractor_1_out;
  wire [4:0] apple_Y, random_2_out, snake_Y, subtractor_2_out;
  wire [7:0] counter_2_q;
  wire [7:2] pull_resistor_2_node;
  wire [7:7] pull_resistor_1_node;
  wire [15:0] score;
  wire [19:0] element_1_out_9, element_2_out_9, element_3_out_9, element_4_out_9, element_5_out_9,
       element_6_out_9, element_7_out_9, element_8_out_9, element_9_out_9, element_10_out_9;

  or or_1 (or_1_out, element_1_boom_2, element_2_boom_2, element_3_boom_2, element_4_boom_2, element_5_boom_2, element_6_boom_2, element_7_boom_2, element_8_boom_2, element_9_boom_2, element_10_boom_2);
  or or_2 (or_2_out, and_1_out, or_1_out, and_2_out);
  and and_1 (and_1_out, in_3[1], ~D___1);  // AND_Gate
  and and_2 (and_2_out, D___1, in_3[2]);
  Decoder #(.select(4), .enable("false")) decoder_1 (
    .out0(decoder_1_out0), .out1(decoder_1_out1), .out2(decoder_1_out2), .out3(decoder_1_out3),
    .out4(decoder_1_out4), .out5(decoder_1_out5), .out6(decoder_1_out6), .out7(decoder_1_out7),
    .out8(decoder_1_out8), .out9(decoder_1_out9), .sel(snake_X));  // open: out10, out11, out12, out13, out14, out15
  assign controlled_buffer_1_out = and_3_out ? in_3[0] : 1'bz;  // Controlled_Buffer controlled_buffer_1
  and and_3 (and_3_out, W___0, not_1_out);
  not not_1 (not_1_out, D___1);
  assign Disp0 = W___0 ? element_1_out_9 : 20'bz;  // Controlled_Buffer controlled_buffer_2
  element element_1 (
    .out_9(element_1_out_9), .snake_X(decoder_1_out0), .snake_Y(snake_Y), .in_2(score), .Tik(Takt),
    .apple_X(decoder_2_out0), .apple_Y(apple_Y), .apple(element_1_apple), .boom_2(element_1_boom_2),
    .boom(D___1));
  Register #(.width(1)) register_1 (.D(not_1_out), .Q(D___1), .clk(not_2_out));  // open: en, clr
  not not_2 (not_2_out, or_2_out);
  assign Disp1 = W___0 ? element_2_out_9 : 20'bz;  // Controlled_Buffer controlled_buffer_3
  element element_2 (
    .out_9(element_2_out_9), .snake_X(decoder_1_out1), .snake_Y(snake_Y), .in_2(score), .Tik(Takt),
    .apple_X(decoder_2_out1), .apple_Y(apple_Y), .apple(element_2_apple), .boom_2(element_2_boom_2),
    .boom(D___1));
  Counter #(.width(16), .max('hffff)) counter_1 (
    .Q(score), .clk(apple), .clr(or_2_out));  // open: load, D, count, carry
  Register #(.width(5)) register_2 (.D(Y___new_Kyda[6:2]), .Q(snake_Y), .clk(X[6]));  // open: en, clr
  Register #(.width(4)) register_3 (.D(X[3:0]), .Q(snake_X), .clk(X[6]));  // open: en, clr
  assign Disp2 = W___0 ? element_3_out_9 : 20'bz;  // Controlled_Buffer controlled_buffer_4
  element element_3 (
    .out_9(element_3_out_9), .snake_X(decoder_1_out2), .snake_Y(snake_Y), .in_2(score), .Tik(Takt),
    .apple_X(decoder_2_out2), .apple_Y(apple_Y), .apple(element_3_apple), .boom_2(element_3_boom_2),
    .boom(D___1));
  // Probe on Kyda
  BitFinder #(.width(4)) bitfinder_1 (.in(S___3), .index(bitfinder_1_index), .found(bitfinder_1_found));
  Register #(.width(2), .trigger("high")) register_4 (
    .D(bitfinder_1_index), .Q(Kyda), .clk(bitfinder_1_found));  // open: en, clr
  assign Disp3 = W___0 ? element_4_out_9 : 20'bz;  // Controlled_Buffer controlled_buffer_5
  element element_4 (
    .out_9(element_4_out_9), .snake_X(decoder_1_out3), .snake_Y(snake_Y), .in_2(score), .Tik(Takt),
    .apple_X(decoder_2_out3), .apple_Y(apple_Y), .apple(element_4_apple), .boom_2(element_4_boom_2),
    .boom(D___1));
  Counter counter_2 (
    .Q(counter_2_q), .clk(controlled_buffer_1_out), .clr(comparator_1_eq));  // open: load, D, count, carry
  assign out_20 = W___0 ? Tik : 1'bz;  // Controlled_Buffer controlled_buffer_6
  Register #(.width(2)) register_5 (.D(Y___new_Kyda[1:0]), .Q(Old_Kyda), .clk(X[6]));  // open: en, clr
  Register #(.width(1)) register_6 (.D(Tik), .Q(Takt), .clk(X[6]), .clr(not_3_out));  // open: en
  not not_3 (not_3_out, Tik);
  assign Disp4 = W___0 ? element_5_out_9 : 20'bz;  // Controlled_Buffer controlled_buffer_7
  element element_5 (
    .out_9(element_5_out_9), .snake_X(decoder_1_out4), .snake_Y(snake_Y), .in_2(score), .Tik(Takt),
    .apple_X(decoder_2_out4), .apple_Y(apple_Y), .apple(element_5_apple), .boom_2(element_5_boom_2),
    .boom(D___1));
  not not_4 (not_4_out, Tik);
  Register #(.width(1)) register_7 (.D(not_4_out), .Q(Tik), .clk(comparator_1_eq), .clr(D___1));  // open: en
  Comparator comparator_1 (.a(counter_2_q), .b(8'hc0), .eq(comparator_1_eq));  // open: gt, lt
  assign Y___new_Kyda_2 = W___0 ? {pull_resistor_1_node[7], snake_Y, Kyda} : 8'bz;  // Controlled_Buffer controlled_buffer_8
  Pull_Resistor pull_resistor_1 (.node({pull_resistor_1_node[7], snake_Y, Kyda}));
  assign Disp5 = W___0 ? element_6_out_9 : 20'bz;  // Controlled_Buffer controlled_buffer_9
  element element_6 (
    .out_9(element_6_out_9), .snake_X(decoder_1_out5), .snake_Y(snake_Y), .in_2(score), .Tik(Takt),
    .apple_X(decoder_2_out5), .apple_Y(apple_Y), .apple(element_6_apple), .boom_2(element_6_boom_2),
    .boom(D___1));
  assign X___old_Kyda = W___0 ? {pull_resistor_2_node[7], snake_X, pull_resistor_2_node[2], Old_Kyda} : 8'bz;  // Controlled_Buffer controlled_buffer_10
  Pull_Resistor pull_resistor_2 (.node({pull_resistor_2_node[7], snake_X, pull_resistor_2_node[2], Old_Kyda}));
  assign Disp6 = W___0 ? element_7_out_9 : 20'bz;  // Controlled_Buffer controlled_buffer_11
  element element_7 (
    .out_9(element_7_out_9), .snake_X(decoder_1_out6), .snake_Y(snake_Y), .in_2(score), .Tik(Takt),
    .apple_X(decoder_2_out6), .apple_Y(apple_Y), .apple(element_7_apple), .boom_2(element_7_boom_2),
    .boom(D___1));
  assign controlled_buffer_12_out = apple ? controlled_buffer_1_out : 1'bz;  // Controlled_Buffer controlled_buffer_12
  assign Disp7 = W___0 ? element_8_out_9 : 20'bz;  // Controlled_Buffer controlled_buffer_13
  element element_8 (
    .out_9(element_8_out_9), .snake_X(decoder_1_out7), .snake_Y(snake_Y), .in_2(score), .Tik(Takt),
    .apple_X(decoder_2_out7), .apple_Y(apple_Y), .apple(element_8_apple), .boom_2(element_8_boom_2),
    .boom(D___1));
  Random #(.width(4)) random_1 (.clk(controlled_buffer_12_out), .out(random_1_out));  // open: next, clr
  Random #(.width(5)) random_2 (.clk(controlled_buffer_12_out), .out(random_2_out));  // open: next, clr
  assign Disp8 = W___0 ? element_9_out_9 : 20'bz;  // Controlled_Buffer controlled_buffer_14
  element element_9 (
    .out_9(element_9_out_9), .snake_X(decoder_1_out8), .snake_Y(snake_Y), .in_2(score), .Tik(Takt),
    .apple_X(decoder_2_out8), .apple_Y(apple_Y), .apple(element_9_apple), .boom_2(element_9_boom_2),
    .boom(D___1));
  Subtractor #(.width(4)) subtractor_1 (.a(random_1_out), .b(4'b1010), .out(subtractor_1_out));  // open: bin, bout
  Comparator #(.width(4), .mode("unsigned")) comparator_2 (
    .a(random_1_out), .b(4'b1001), .gt(comparator_2_gt));  // open: eq, lt
  Subtractor #(.width(5)) subtractor_2 (.a(random_2_out), .b(5'b10100), .out(subtractor_2_out));  // open: bin, bout
  Comparator #(.width(5), .mode("unsigned")) comparator_3 (
    .a(random_2_out), .b(5'b10011), .gt(comparator_3_gt));  // open: eq, lt
  assign Disp9 = W___0 ? element_10_out_9 : 20'bz;  // Controlled_Buffer controlled_buffer_15
  element element_10 (
    .out_9(element_10_out_9), .snake_X(decoder_1_out9), .snake_Y(snake_Y), .in_2(score), .Tik(Takt),
    .apple_X(decoder_2_out9), .apple_Y(apple_Y), .apple(element_10_apple), .boom_2(element_10_boom_2),
    .boom(D___1));
  Decoder #(.select(4), .enable("false")) decoder_2 (
    .out0(decoder_2_out0), .out1(decoder_2_out1), .out2(decoder_2_out2), .out3(decoder_2_out3),
    .out4(decoder_2_out4), .out5(decoder_2_out5), .out6(decoder_2_out6), .out7(decoder_2_out7),
    .out8(decoder_2_out8), .out9(decoder_2_out9), .sel(multiplexer_1_out));  // open: out10, out11, out12, out13, out14, out15
  Multiplexer #(.width(4), .enable("false")) multiplexer_1 (
    .in0(random_1_out), .in1(subtractor_1_out), .out(multiplexer_1_out), .sel(comparator_2_gt));
  Multiplexer #(.width(5), .enable("false")) multiplexer_2 (
    .in0(random_2_out), .in1(subtractor_2_out), .out(apple_Y), .sel(comparator_3_gt));
  or or_3 (or_3_out, element_1_apple, element_2_apple, element_3_apple, element_4_apple, element_5_apple, element_6_apple, element_7_apple, element_8_apple, element_9_apple, element_10_apple);
  not not_5 (apple, or_3_out);
  assign out_16 = W___0 ? score : 16'bz;  // Controlled_Buffer controlled_buffer_16

  // Other names for the same wires on the sheet: New_X[3:0] = X[3:0]; res = D___1; sel = W___0;
  //   New_Y[4:0] = Y___new_Kyda[6:2]

  // Notes on the sheet:
  //   A = 2
endmodule

module \bit  (
  input  in,
  input  [15:0] score,
  input  in_3,
  input  tik,
  output out
);

  wire comparator_1_eq, controlled_buffer_1_out, or_1_out;
  wire [15:0] counter_1_q;

  assign controlled_buffer_1_out = out ? tik : 1'bz;  // Controlled_Buffer controlled_buffer_1
  Comparator #(.width(16), .mode("unsigned")) comparator_1 (
    .a(score), .b(counter_1_q), .eq(comparator_1_eq));  // open: gt, lt
  Counter #(.width(16), .max('hffff)) counter_1 (
    .Q(counter_1_q), .clk(controlled_buffer_1_out), .clr(or_1_out));  // open: load, D, count, carry
  Register #(.width(1)) register_1 (.D(in), .Q(out), .clk(in), .clr(or_1_out));  // open: en
  or or_1 (or_1_out, comparator_1_eq, in_3);
endmodule

module element (
  input  boom,
  input  [15:0] in_2,
  input  Tik,
  input  [4:0] apple_Y,
  input  apple_X,
  input  snake_X,
  input  [4:0] snake_Y,
  output boom_2,
  output [19:0] out_9,
  output apple
);

  wire comparator_1_eq, comparator_2_eq;
  wire [19:0] and_1_out, and_2_out, bit_1_out, decoder_1_out0, multiplexer_1_out, multiplexer_2_out,
       or_1_out, or_2_out, or_3_out, or_4_out, pull_resistor_1_node, register_1_q, shifter_1_out;

  Decoder #(.select(5), .disabled(0)) decoder_1 (
    .out0(decoder_1_out0[0]), .out1(decoder_1_out0[1]), .out2(decoder_1_out0[2]), .out3(decoder_1_out0[3]),
    .out4(decoder_1_out0[4]), .out5(decoder_1_out0[5]), .out6(decoder_1_out0[6]), .out7(decoder_1_out0[7]),
    .out8(decoder_1_out0[8]), .out9(decoder_1_out0[9]), .out10(decoder_1_out0[10]),
    .out11(decoder_1_out0[11]), .out12(decoder_1_out0[12]), .out13(decoder_1_out0[13]),
    .out14(decoder_1_out0[14]), .out15(decoder_1_out0[15]), .out16(decoder_1_out0[16]),
    .out17(decoder_1_out0[17]), .out18(decoder_1_out0[18]), .out19(decoder_1_out0[19]), .sel(snake_Y),
    .en(snake_X));  // open: out20, out21, out22, out23, out24, out25, out26, out27, out28, out29, out30, out31
  \bit  bit_1 (.in(multiplexer_1_out[0]), .score(in_2), .tik(Tik), .out(bit_1_out[0]), .in_3(boom));
  \bit  bit_2 (.in(multiplexer_1_out[1]), .score(in_2), .tik(Tik), .out(bit_1_out[1]), .in_3(boom));
  \bit  bit_3 (.in(multiplexer_1_out[2]), .score(in_2), .tik(Tik), .out(bit_1_out[2]), .in_3(boom));
  \bit  bit_4 (.in(multiplexer_1_out[3]), .score(in_2), .tik(Tik), .out(bit_1_out[3]), .in_3(boom));
  \bit  bit_5 (.in(multiplexer_1_out[4]), .score(in_2), .tik(Tik), .out(bit_1_out[4]), .in_3(boom));
  \bit  bit_6 (.in(multiplexer_1_out[5]), .score(in_2), .tik(Tik), .out(bit_1_out[5]), .in_3(boom));
  \bit  bit_7 (.in(multiplexer_1_out[6]), .score(in_2), .tik(Tik), .out(bit_1_out[6]), .in_3(boom));
  \bit  bit_8 (.in(multiplexer_1_out[7]), .score(in_2), .tik(Tik), .out(bit_1_out[7]), .in_3(boom));
  \bit  bit_9 (.in(multiplexer_1_out[8]), .score(in_2), .tik(Tik), .out(bit_1_out[8]), .in_3(boom));
  \bit  bit_10 (.in(multiplexer_1_out[9]), .score(in_2), .tik(Tik), .out(bit_1_out[9]), .in_3(boom));
  \bit  bit_11 (.in(multiplexer_1_out[10]), .score(in_2), .tik(Tik), .out(bit_1_out[10]), .in_3(boom));
  \bit  bit_12 (.in(multiplexer_1_out[11]), .score(in_2), .tik(Tik), .out(bit_1_out[11]), .in_3(boom));
  \bit  bit_13 (.in(multiplexer_1_out[12]), .score(in_2), .tik(Tik), .out(bit_1_out[12]), .in_3(boom));
  \bit  bit_14 (.in(multiplexer_1_out[13]), .score(in_2), .tik(Tik), .out(bit_1_out[13]), .in_3(boom));
  \bit  bit_15 (.in(multiplexer_1_out[14]), .score(in_2), .tik(Tik), .out(bit_1_out[14]), .in_3(boom));
  \bit  bit_16 (.in(multiplexer_1_out[15]), .score(in_2), .tik(Tik), .out(bit_1_out[15]), .in_3(boom));
  \bit  bit_17 (.in(multiplexer_1_out[16]), .score(in_2), .tik(Tik), .out(bit_1_out[16]), .in_3(boom));
  \bit  bit_18 (.in(multiplexer_1_out[17]), .score(in_2), .tik(Tik), .out(bit_1_out[17]), .in_3(boom));
  \bit  bit_19 (.in(multiplexer_1_out[18]), .score(in_2), .tik(Tik), .out(bit_1_out[18]), .in_3(boom));
  \bit  bit_20 (.in(multiplexer_1_out[19]), .score(in_2), .tik(Tik), .out(bit_1_out[19]), .in_3(boom));
  Pull_Resistor pull_resistor_1 (.node(pull_resistor_1_node));
  Shifter #(.width(20)) shifter_1 (.in(20'h1), .\dist (apple_Y), .out(shifter_1_out));
  assign pull_resistor_1_node = apple_X ? shifter_1_out : 20'bz;  // Controlled_Buffer controlled_buffer_1
  assign and_1_out = bit_1_out & decoder_1_out0;  // AND_Gate and_1, 20 bits wide
  assign or_1_out = bit_1_out | decoder_1_out0;  // OR_Gate or_1, 20 bits wide
  assign and_2_out = multiplexer_1_out & pull_resistor_1_node;  // AND_Gate and_2, 20 bits wide
  assign or_2_out = multiplexer_1_out | pull_resistor_1_node;  // OR_Gate or_2, 20 bits wide
  Pull_Resistor pull_resistor_2 (.node(boom_2));
  not not_1 (boom_2, comparator_1_eq);
  Comparator #(.width(20)) comparator_1 (.a({20{1'b0}}), .b(and_1_out), .eq(comparator_1_eq));  // open: gt, lt
  Comparator #(.width(20)) comparator_2 (.a(and_2_out), .b({20{1'b0}}), .eq(comparator_2_eq));  // open: gt, lt
  Register #(.width(20)) register_1 (.D(or_1_out), .Q(register_1_q), .clk(Tik));  // open: en, clr
  Multiplexer #(.width(20), .enable("false")) multiplexer_1 (
    .in0(register_1_q), .in1(decoder_1_out0), .out(multiplexer_1_out), .sel(boom));
  and and_3 (apple, comparator_2_eq, apple_X);
  assign or_3_out = decoder_1_out0 | multiplexer_1_out;  // OR_Gate or_3, 20 bits wide
  assign or_4_out = decoder_1_out0 | or_2_out;  // OR_Gate or_4, 20 bits wide
  assign out_9 = or_3_out;  // Buffer buffer_1, 20 bits wide
  Multiplexer #(.width(20), .enable("false")) multiplexer_2 (
    .in0(or_3_out), .in1(or_4_out), .out(multiplexer_2_out), .sel(apple));
  assign out_9 = multiplexer_2_out;  // Buffer buffer_2, 20 bits wide
endmodule
